// Logisim project Base1.circ as structural Verilog: 27 circuits, main circuit main
module main (
  input  in_1,
  input  in_2,
  input  in_3,
  output out_4
);

  Seletor seletor_1 (.A(in_1), .S(in_2), .B(in_3), .C(out_4));
endmodule

module XOR (
  input  A,
  input  B,
  output A_XOR_B
);

  wire and_1_out, and_2_out, not_1_out, not_2_out;

  not not_1 (not_1_out, B);
  not not_2 (not_2_out, A);
  and and_1 (and_1_out, A, not_1_out);
  and and_2 (and_2_out, not_2_out, B);
  or or_1 (A_XOR_B, and_1_out, and_2_out);

  // Notes on the sheet:
  //   XOR = (A . (-B) ) + ( (-A) . B)
endmodule

module Somador_de_bits (
  input  C0,
  input  A0,
  input  B0,
  output S0,
  output C1
);

  wire and_1_out, and_2_out, xor_1_a_xor_b;

  XOR xor_1 (.A(C0), .B(A0), .A_XOR_B(xor_1_a_xor_b));
  and and_1 (and_1_out, C0, A0);
  and and_2 (and_2_out, xor_1_a_xor_b, B0);
  XOR xor_2 (.A(xor_1_a_xor_b), .B(B0), .A_XOR_B(S0));
  or or_1 (C1, and_1_out, and_2_out);

  // Notes on the sheet:
  //   Somador de bits
endmodule

module Somador_de_4_bits (
  input  A3,
  input  A2,
  input  A1,
  input  A0,
  input  B3,
  input  B2,
  input  B1,
  input  B0,
  output S4,
  output S3,
  output S2,
  output S1,
  output S0
);

  wire somador_de_bits_2_c1, somador_de_bits_3_c1, somador_de_bits_4_c1;

  Somador_de_bits somador_de_bits_1 (.C0(somador_de_bits_2_c1), .A0(A3), .B0(B3), .S0(S3), .C1(S4));
  Somador_de_bits somador_de_bits_2 (.C0(somador_de_bits_3_c1), .A0(A2), .B0(B2), .S0(S2), .C1(somador_de_bits_2_c1));
  Somador_de_bits somador_de_bits_3 (.C0(somador_de_bits_4_c1), .A0(A1), .B0(B1), .S0(S1), .C1(somador_de_bits_3_c1));
  Somador_de_bits somador_de_bits_4 (.C0(1'b0), .A0(A0), .B0(B0), .S0(S0), .C1(somador_de_bits_4_c1));

  // Notes on the sheet:
  //   Somador de 4 bits
endmodule

module Somador_de_4_bits_1_saida (
  input  in_1,
  input  in_2,
  input  in_3,
  input  in_4,
  input  in_5,
  input  in_6,
  input  in_7,
  input  in_8,
  output [4:0] out_9
);

  wire somador_de_bits_2_c1, somador_de_bits_3_c1, somador_de_bits_4_c1;

  Somador_de_bits somador_de_bits_1 (.C0(somador_de_bits_2_c1), .A0(in_1), .B0(in_5), .S0(out_9[3]), .C1(out_9[4]));
  Somador_de_bits somador_de_bits_2 (
    .C0(somador_de_bits_3_c1), .A0(in_2), .B0(in_6), .S0(out_9[2]), .C1(somador_de_bits_2_c1));
  Somador_de_bits somador_de_bits_3 (
    .C0(somador_de_bits_4_c1), .A0(in_3), .B0(in_7), .S0(out_9[1]), .C1(somador_de_bits_3_c1));
  Somador_de_bits somador_de_bits_4 (.C0(1'b0), .A0(in_4), .B0(in_8), .S0(out_9[0]), .C1(somador_de_bits_4_c1));

  // Notes on the sheet:
  //   Somador de 4 bits com 1 saída
endmodule

module Seletor (
  input  A,
  input  S,
  input  B,
  output C
);

  wire and_1_out, and_2_out, not_1_out;

  not not_1 (not_1_out, S);
  and and_1 (and_1_out, A, not_1_out);
  and and_2 (and_2_out, S, B);
  or or_1 (C, and_1_out, and_2_out);

  // Notes on the sheet:
  //   Seletor otimizado
endmodule

module Seletor_4_bits (
  input  A0,
  input  B0,
  input  A1,
  input  B1,
  input  S,
  input  A2,
  input  B2,
  input  A3,
  input  B3,
  output [3:0] C
);

  Seletor seletor_1 (.A(A0), .S(S), .B(B0), .C(C[0]));
  Seletor seletor_2 (.A(A1), .S(S), .B(B1), .C(C[1]));
  Seletor seletor_3 (.A(A2), .S(S), .B(B2), .C(C[2]));
  Seletor seletor_4 (.A(A3), .S(S), .B(B3), .C(C[3]));

  // Notes on the sheet:
  //   Seletor_Simples
endmodule

module Seletor_4_bits_personalizado (
  input  A0,
  input  B0,
  input  A1,
  input  B1,
  input  S,
  input  A2,
  input  B2,
  input  A3,
  input  B3,
  output [3:0] A,
  output [3:0] C,
  output [3:0] B
);

  Seletor seletor_1 (.A(A0), .S(S), .B(B0), .C(C[0]));
  Seletor seletor_2 (.A(A1), .S(S), .B(B1), .C(C[1]));
  Seletor seletor_3 (.A(A2), .S(S), .B(B2), .C(C[2]));
  Seletor seletor_4 (.A(A3), .S(S), .B(B3), .C(C[3]));

  assign A = {A3, A2, A1, A0};
  assign B = {B3, B2, B1, B0};

  // Notes on the sheet:
  //   Seletor_Personalizado
endmodule

module Projeto_parte_1 (
  input  A3,
  input  A2,
  input  A1,
  input  A0,
  input  S,
  input  B3,
  input  B2,
  input  B1,
  input  B0,
  output [3:0] A,
  output [3:0] C,
  output [3:0] B
);

  Seletor_4_bits_personalizado seletor_4_bits_personalizado_1 (
    .A(A), .S(S), .B(B), .A3(A3), .A2(A2), .A1(A1), .A0(A0), .B3(B3), .B2(B2), .B1(B1), .B0(B0), .C(C));

  // Notes on the sheet:
  //   Projeto
endmodule

module Exerc4_10a (
  input  in_1,
  input  in_2,
  input  in_3,
  input  in_4,
  output out_5
);

  and and_1 (out_5, in_1, in_2, in_3, in_4);

  // Notes on the sheet:
  //   Y = A x B x C x D
endmodule

module Exerc4_10b (
  input  in_1,
  input  in_2,
  input  in_3,
  input  in_4,
  output out_5
);

  or or_1 (out_5, in_1, in_2, in_3, in_4);

  // Notes on the sheet:
  //   Y = A + B + C + D
endmodule

module Exerc4_10c (
  input  in_1,
  input  in_2,
  input  in_3,
  input  in_4,
  input  in_5,
  output out_6
);

  wire and_1_out, and_2_out;

  and and_1 (and_1_out, in_1, in_2);
  and and_2 (and_2_out, in_3, in_4, in_5);
  or or_1 (out_6, and_1_out, and_2_out);

  // Notes on the sheet:
  //   Y = AxB + CxDxE
endmodule

module Exerc4_10d (
  input  in_1,
  input  in_2,
  input  in_3,
  input  in_4,
  input  in_5,
  output out_6
);

  wire or_1_out, or_2_out;

  or or_1 (or_1_out, in_1, in_2);
  or or_2 (or_2_out, in_3, in_4, in_5);
  and and_1 (out_6, or_1_out, or_2_out);

  // Notes on the sheet:
  //   Y = (A + B) x (C + D + E)
endmodule

module Exerc4_11a (
  input  in_1,
  input  in_2,
  input  in_3,
  input  in_4,
  output out_5
);

  wire and_1_out, and_2_out;

  and and_1 (and_1_out, in_1, in_2);
  and and_2 (and_2_out, in_3, in_4);
  and and_3 (out_5, and_1_out, and_2_out);

  // Notes on the sheet:
  //   Y = A x B x C x D
endmodule

module Exerc4_11b (
  input  in_1,
  input  in_2,
  input  in_3,
  input  in_4,
  output out_5
);

  wire or_1_out, or_2_out;

  or or_1 (or_1_out, in_1, in_2);
  or or_2 (or_2_out, in_3, in_4);
  or or_3 (out_5, or_1_out, or_2_out);

  // Notes on the sheet:
  //   Y = A + B + C + D
endmodule

module Exerc4_11c (
  input  in_1,
  input  in_2,
  input  in_3,
  input  in_4,
  input  in_5,
  output out_6
);

  wire and_1_out, and_2_out, and_3_out;

  and and_1 (and_1_out, in_3, in_4);
  and and_2 (and_2_out, in_1, in_2);
  and and_3 (and_3_out, and_1_out, in_5);
  or or_1 (out_6, and_2_out, and_3_out);

  // Notes on the sheet:
  //   Y = A x B + C x D x E
endmodule

module Exerc4_11d (
  input  in_1,
  input  in_2,
  input  in_3,
  input  in_4,
  input  in_5,
  output out_6
);

  wire or_1_out, or_2_out, or_3_out;

  or or_1 (or_1_out, in_3, in_4);
  or or_2 (or_2_out, in_1, in_2);
  or or_3 (or_3_out, or_1_out, in_5);
  and and_1 (out_6, or_2_out, or_3_out);

  // Notes on the sheet:
  //   Y = (A + B) x (C + D + E)
endmodule

module Display (
);

  wire display_intermediario_1_a, display_intermediario_1_b, display_intermediario_1_out_4,
       display_intermediario_1_out_5, display_intermediario_1_out_6, display_intermediario_1_out_7,
       display_intermediario_1_out_8;

  Display_intermediario display_intermediario_1 (
    .A(display_intermediario_1_a), .B(display_intermediario_1_b), .out_4(display_intermediario_1_out_4),
    .out_5(display_intermediario_1_out_5), .out_6(display_intermediario_1_out_6),
    .out_7(display_intermediario_1_out_7), .out_8(display_intermediario_1_out_8));  // open: in_1
  _7_Segment_Display u_7_segment_display_1 (
    .g(display_intermediario_1_out_5), .f(display_intermediario_1_out_4), .a(display_intermediario_1_b),
    .b(display_intermediario_1_a), .e(display_intermediario_1_out_6), .d(display_intermediario_1_out_7),
    .c(display_intermediario_1_out_8));  // open: dp

  // Notes on the sheet:
  //   A
  //   B
  //   C
  //   D
  //   E
  //   F
  //   G
endmodule

module Display_intermediario (
  input  [3:0] in_1,
  output A,
  output B,
  output out_4,
  output out_5,
  output out_6,
  output out_7,
  output out_8
);

  Display_a display_a_1 (.in_1(in_1), .A(A));
  Display_b display_b_1 (.A(in_1), .out_2(B));
  Display_c display_c_1 (.in_1(in_1), .out_2(out_4));
  Display_d display_d_1 (.in_1(in_1), .out_2(out_5));
  Display_e display_e_1 (.in_1(in_1), .out_2(out_6));
  Display_f display_f_1 (.in_1(in_1), .out_2(out_7));
  Display_g display_g_1 (.in_1(in_1), .out_2(out_8));
endmodule

module Display_a (
  input  [3:0] in_1,
  output A
);

  wire and_1_out, and_2_out, and_3_out, and_4_out, and_5_out;

  and and_1 (and_1_out, ~in_1[0], ~in_1[2]);  // AND_Gate
  and and_2 (and_2_out, in_1[0], ~in_1[1], in_1[3]);  // AND_Gate
  and and_3 (and_3_out, in_1[0], in_1[1], ~in_1[3]);  // AND_Gate
  and and_4 (and_4_out, ~in_1[1], ~in_1[2]);  // AND_Gate
  and and_5 (and_5_out, ~in_1[0], ~in_1[1], ~in_1[3]);  // AND_Gate
  or or_1 (A, and_1_out, and_2_out, and_3_out, and_4_out, and_5_out);

  // Notes on the sheet:
  //   -B-D + A-CD + -ACD + -B-C + -A-C-D
  //   D
  //   C
  //   B
  //   A
  //   -B-C
endmodule

module Display_b (
  input  [3:0] A,
  output out_2
);

  wire and_1_out, and_2_out, and_3_out, and_4_out, and_5_out, and_6_out;

  and and_1 (and_1_out, A[1], ~A[3]);  // AND_Gate
  and and_2 (and_2_out, ~A[1], ~A[2], A[3]);  // AND_Gate
  and and_3 (and_3_out, A[0], A[2], ~A[3]);  // AND_Gate
  and and_4 (and_4_out, ~A[0], ~A[1], ~A[2]);  // AND_Gate
  and and_5 (and_5_out, ~A[0], A[3]);  // AND_Gate
  and and_6 (and_6_out, A[1], A[2], A[3]);
  or or_1 (out_2, and_2_out, and_4_out, and_5_out, and_6_out, and_3_out, and_1_out);

  // Notes on the sheet:
  //   -AC + -ABD + ABC + A-D + -B-C-D + A-B-C
  //   D
  //   C
  //   B
endmodule

module Display_c (
  input  [3:0] in_1,
  output out_2
);

  // OR_Gate or_1 has open pins: out=out_2

  // Notes on the sheet:
  //   -C-D + -AB-C + A-B + AC + B-D
endmodule

module Display_d (
  input  [3:0] in_1,
  output out_2
);

  // OR_Gate or_1 has open pins: out=out_2
endmodule

module Display_e (
  input  [3:0] in_1,
  output out_2
);

  // OR_Gate or_1 has open pins: out=out_2
endmodule

module Display_f (
  input  [3:0] in_1,
  output out_2
);

  // OR_Gate or_1 has open pins: out=out_2
endmodule

module Display_g (
  input  [3:0] in_1,
  output out_2
);

  // OR_Gate or_1 has open pins: out=out_2
endmodule

module PRIMO (
  input  A,
  input  B,
  input  C,
  input  D,
  output out_5
);

  wire and_1_out, and_2_out, and_3_out, and_4_out;

  and and_1 (and_1_out, ~A, ~B, C);  // AND_Gate
  and and_2 (and_2_out, ~A, B, D);  // AND_Gate
  and and_3 (and_3_out, B, ~C, D);  // AND_Gate
  and and_4 (and_4_out, ~B, C, D);  // AND_Gate
  or or_1 (out_5, and_1_out, and_2_out, and_3_out, and_4_out);

  // Notes on the sheet:
  //   NÚMERO PRIMO
endmodule
