// Logisim project Base2.circ as structural Verilog
module Circuito_de_memoria_RS_1 (
  input  R,
  input  S,
  output Q,
  output Q_cdbbc008
);

  nor nor_1 (Q, R, Q_cdbbc008);
  nor nor_2 (Q_cdbbc008, Q, S);

  // Notes on the sheet:
  //   CIRCUITO DE MEMORIA RS 1
endmodule

module Circuito_de_memoria_RS_2 (
  input  R,
  input  CLOCK,
  input  S,
  output Q,
  output Q_cdbbc008
);

  wire and_1_out, and_2_out;

  and and_1 (and_1_out, R, CLOCK);
  and and_2 (and_2_out, CLOCK, S);
  nor nor_1 (Q, and_1_out, Q_cdbbc008);
  nor nor_2 (Q_cdbbc008, Q, and_2_out);

  // Notes on the sheet:
  //   CIRCUITO DE MEMORIA RS 2
endmodule

module Circuito_de_memoria_D_1 (
  input  D,
  input  CLOCK,
  output Q,
  output Q_cdbbc008
);

  wire and_1_out, and_2_out, not_1_out;

  not not_1 (not_1_out, D);
  and and_1 (and_1_out, not_1_out, CLOCK);
  and and_2 (and_2_out, CLOCK, D);
  nor nor_1 (Q, and_1_out, Q_cdbbc008);
  nor nor_2 (Q_cdbbc008, Q, and_2_out);

  // Notes on the sheet:
  //   CIRCUITO DE MEMORIA D 1
endmodule

module Circuito_de_memoria_D_2 (
  input  D,
  input  CLOCK,
  output Q,
  output Q_cdbbc008
);

  wire and_1_out, and_2_out, and_3_out, not_1_out, not_2_out;

  not not_1 (not_1_out, CLOCK);
  and and_1 (and_1_out, not_1_out, CLOCK);
  not not_2 (not_2_out, D);
  and and_2 (and_2_out, not_2_out, and_1_out);
  and and_3 (and_3_out, and_1_out, D);
  nor nor_1 (Q, and_2_out, Q_cdbbc008);
  nor nor_2 (Q_cdbbc008, Q, and_3_out);

  // Notes on the sheet:
  //   CIRCUITO DE MEMORIA D 2 - não funciona no simulador, mas na vida real sim
endmodule

module Circuito_de_memoria_D_3 (
  input  D,
  input  CLOCK,
  output Q,
  output Q_cdbbc008
);

  wire and_1_out, and_2_out, and_3_out, not_1_out, not_2_out, not_3_out, not_4_out;

  not not_1 (not_1_out, not_2_out);
  not not_2 (not_2_out, CLOCK);
  not not_3 (not_3_out, not_1_out);
  and and_1 (and_1_out, not_3_out, CLOCK);
  not not_4 (not_4_out, D);
  and and_2 (and_2_out, not_4_out, and_1_out);
  and and_3 (and_3_out, and_1_out, D);
  nor nor_1 (Q, and_2_out, Q_cdbbc008);
  nor nor_2 (Q_cdbbc008, Q, and_3_out);

  // Notes on the sheet:
  //   CIRCUITO DE MEMORIA D 2 - funciona no simulador e na vida real sim
endmodule

module Constante (
  input  in_1
);

  wire or_1_out;

  or or_1 (or_1_out, in_1, 1'b1);
endmodule

module Registrador (
  input  in_1,
  input  [3:0] in_2,
  output [3:0] out_3
);

  D_Flip_Flop d_ff_1 (.D(in_2[3]), .clk(in_1), .Q(out_3[3]));  // open: Qn, preset, reset
  D_Flip_Flop d_ff_2 (.D(in_2[2]), .clk(in_1), .Q(out_3[2]));  // open: Qn, preset, reset
  D_Flip_Flop d_ff_3 (.D(in_2[1]), .clk(in_1), .Q(out_3[1]));  // open: Qn, preset, reset
  D_Flip_Flop d_ff_4 (.D(in_2[0]), .clk(in_1), .Q(out_3[0]));  // open: Qn, preset, reset
endmodule
