// Logisim project Projeto1.circ as structural Verilog: 24 circuits, main circuit main
module main (
  input  A3,
  input  A2,
  input  A1,
  input  A0,
  input  Jogar,
  input  S,
  input  B3,
  input  B2,
  input  B1,
  input  B0
);

  wire display_intermediario_1_a, display_intermediario_1_b, display_intermediario_1_c,
       display_intermediario_1_d, display_intermediario_1_e, display_intermediario_1_f,
       display_intermediario_1_g, display_intermediario_2_a, display_intermediario_2_b,
       display_intermediario_2_c, display_intermediario_2_d, display_intermediario_2_e,
       display_intermediario_2_f, display_intermediario_2_g, game_1_out_3, game_1_out_4, game_1_out_5;
  wire [3:0] seletor_4_bits_personalizado_1_a, seletor_4_bits_personalizado_1_b,
       seletor_4_bits_personalizado_1_c;

  _7_Segment_Display u_7_segment_display_1 (
    .g(display_intermediario_1_d), .f(display_intermediario_1_c), .a(display_intermediario_1_b),
    .b(display_intermediario_1_a), .e(display_intermediario_1_e), .d(display_intermediario_1_f),
    .c(display_intermediario_1_g));  // open: dp
  _7_Segment_Display u_7_segment_display_2 (
    .g(display_intermediario_2_d), .f(display_intermediario_2_c), .a(display_intermediario_2_b),
    .b(display_intermediario_2_a), .e(display_intermediario_2_e), .d(display_intermediario_2_f),
    .c(display_intermediario_2_g));  // open: dp
  Display_intermediario display_intermediario_1 (
    .in_1(seletor_4_bits_personalizado_1_a), .A(display_intermediario_1_a), .B(display_intermediario_1_b),
    .C(display_intermediario_1_c), .D(display_intermediario_1_d), .E(display_intermediario_1_e),
    .F(display_intermediario_1_f), .G(display_intermediario_1_g));
  Display_intermediario display_intermediario_2 (
    .in_1(seletor_4_bits_personalizado_1_b), .A(display_intermediario_2_a), .B(display_intermediario_2_b),
    .C(display_intermediario_2_c), .D(display_intermediario_2_d), .E(display_intermediario_2_e),
    .F(display_intermediario_2_f), .G(display_intermediario_2_g));
  Seletor_4_bits_personalizado seletor_4_bits_personalizado_1 (
    .A(seletor_4_bits_personalizado_1_a), .S(S), .B(seletor_4_bits_personalizado_1_b), .A3(A3), .A2(A2),
    .A1(A1), .A0(A0), .B3(B3), .B2(B2), .B1(B1), .B0(B0), .C(seletor_4_bits_personalizado_1_c));
  Game game_1 (
    .in_2(seletor_4_bits_personalizado_1_c), .in_1(Jogar), .out_3(game_1_out_3), .out_4(game_1_out_4),
    .out_5(game_1_out_5));
  LED Maior (.in(game_1_out_3));
  LED Igual (.in(game_1_out_4));
  LED Menor (.in(game_1_out_5));

  // Notes on the sheet:
  //   Projeto
  //   decode
  //   game
endmodule

module Seletor (
  input  A,
  input  S,
  input  B,
  output C
);

  wire and_1_out, and_2_out, not_1_out;

  not not_1 (not_1_out, S);
  and and_1 (and_1_out, A, not_1_out);
  and and_2 (and_2_out, S, B);
  or or_1 (C, and_1_out, and_2_out);

  // Notes on the sheet:
  //   Seletor otimizado
endmodule

module Seletor_4_bits (
  input  A0,
  input  B0,
  input  A1,
  input  B1,
  input  S,
  input  A2,
  input  B2,
  input  A3,
  input  B3,
  output [3:0] C
);

  Seletor seletor_1 (.A(A0), .S(S), .B(B0), .C(C[0]));
  Seletor seletor_2 (.A(A1), .S(S), .B(B1), .C(C[1]));
  Seletor seletor_3 (.A(A2), .S(S), .B(B2), .C(C[2]));
  Seletor seletor_4 (.A(A3), .S(S), .B(B3), .C(C[3]));

  // Notes on the sheet:
  //   Seletor_Simples
endmodule

module Seletor_4_bits_personalizado (
  input  A0,
  input  B0,
  input  A1,
  input  B1,
  input  S,
  input  A2,
  input  B2,
  input  A3,
  input  B3,
  output [3:0] A,
  output [3:0] C,
  output [3:0] B
);

  Seletor seletor_1 (.A(A0), .S(S), .B(B0), .C(C[0]));
  Seletor seletor_2 (.A(A1), .S(S), .B(B1), .C(C[1]));
  Seletor seletor_3 (.A(A2), .S(S), .B(B2), .C(C[2]));
  Seletor seletor_4 (.A(A3), .S(S), .B(B3), .C(C[3]));

  assign A = {A3, A2, A1, A0};
  assign B = {B3, B2, B1, B0};

  // Notes on the sheet:
  //   Seletor_Personalizado
endmodule

module Display_intermediario (
  input  [3:0] in_1,
  output A,
  output B,
  output C,
  output D,
  output E,
  output F,
  output G
);

  Display_a display_a_1 (.B(in_1), .A(A));
  Display_b display_b_1 (.A(in_1), .out_2(B));
  Display_c display_c_1 (.A(in_1), .out_2(C));
  Display_d display_d_1 (.in_1(in_1), .out_2(D));
  Display_e display_e_1 (.in_1(in_1), .out_2(E));
  Display_f display_f_1 (.in_1(in_1), .out_2(F));
  Display_g display_g_1 (.in_1(in_1), .out_2(G));

  // Notes on the sheet:
  //   Display Intermediário
endmodule

module Game (
  input  in_1,
  input  [3:0] in_2,
  output out_3,
  output out_4,
  output out_5
);

  wire comparador_1_out_3, comparador_1_out_4, comparador_1_out_5;

  Comparador comparador_1 (
    .Secret(4'b0111), .User(in_2), .out_3(comparador_1_out_3), .out_4(comparador_1_out_4),
    .out_5(comparador_1_out_5));
  and and_1 (out_3, in_1, comparador_1_out_3);
  and and_2 (out_4, in_1, comparador_1_out_4);
  and and_3 (out_5, comparador_1_out_5, in_1);
endmodule

module Comparador (
  input  [3:0] Secret,
  input  [3:0] User,
  output out_3,
  output out_4,
  output out_5
);

  wire comparador_igual_1_s0, comparador_igual_2_s0, comparador_igual_3_s0, comparador_igual_4_s0,
       comparador_maior1_1_maior_a, comparador_maior2_1_out_4, comparador_maior3_1_out_5,
       comparador_maior4_1_out_6;

  comparador_igual comparador_igual_1 (.A0(Secret[3]), .B0(User[3]), .S0(comparador_igual_1_s0));
  Comparador_maior1 comparador_maior1_1 (.A(Secret[3]), .B(User[3]), .Maior_A(comparador_maior1_1_maior_a));
  comparador_igual comparador_igual_2 (.A0(Secret[2]), .B0(User[2]), .S0(comparador_igual_2_s0));
  Comparador_maior2 comparador_maior2_1 (
    .A2(Secret[2]), .I3(comparador_igual_1_s0), .B2(User[2]), .out_4(comparador_maior2_1_out_4));
  Comparador_maior3 comparador_maior3_1 (
    .A1(Secret[1]), .I2(comparador_igual_2_s0), .I3(comparador_igual_1_s0), .B1(User[1]),
    .out_5(comparador_maior3_1_out_5));
  comparador_igual comparador_igual_3 (.A0(Secret[1]), .B0(User[1]), .S0(comparador_igual_3_s0));
  comparador_igual comparador_igual_4 (.A0(Secret[0]), .B0(User[0]), .S0(comparador_igual_4_s0));
  Comparador_maior4 comparador_maior4_1 (
    .A0(Secret[0]), .I1(comparador_igual_3_s0), .I2(comparador_igual_2_s0), .I3(comparador_igual_1_s0),
    .B0(User[0]), .out_6(comparador_maior4_1_out_6));
  or or_1 (out_3, comparador_maior1_1_maior_a, comparador_maior2_1_out_4, comparador_maior3_1_out_5, comparador_maior4_1_out_6);
  and and_1 (out_4, comparador_igual_1_s0, comparador_igual_2_s0, comparador_igual_3_s0, comparador_igual_4_s0);
  and and_2 (out_5, ~out_3, ~out_4);  // AND_Gate
endmodule

// Igual
module comparador_igual (
  input  A0,
  input  B0,
  output S0
);

  wire and_1_out, and_2_out;

  and and_1 (and_1_out, ~A0, ~B0);  // AND_Gate
  and and_2 (and_2_out, A0, B0);
  or or_1 (S0, and_1_out, and_2_out);

  // Notes on the sheet:
  //   XNOR
endmodule

module Comparador_1bit (
  input  in_1,
  input  in_2,
  output out_3
);

  and and_1 (out_3, in_1, ~in_2);  // AND_Gate
endmodule

// Maior
module Comparador_maior1 (
  input  A,
  input  B,
  output Maior_A
);

  and and_1 (Maior_A, A, ~B);  // AND_Gate
endmodule

// Maior
module Comparador_maior2 (
  input  A2,
  input  I3,
  input  B2,
  output out_4
);

  wire comparador_maior1_1_maior_a;

  Comparador_maior1 comparador_maior1_1 (.A(A2), .B(B2), .Maior_A(comparador_maior1_1_maior_a));
  and and_1 (out_4, I3, comparador_maior1_1_maior_a);
endmodule

// Maior
module Comparador_maior3 (
  input  A1,
  input  I2,
  input  I3,
  input  B1,
  output out_5
);

  wire comparador_maior1_1_maior_a;

  Comparador_maior1 comparador_maior1_1 (.A(A1), .B(B1), .Maior_A(comparador_maior1_1_maior_a));
  and and_1 (out_5, I2, I3, comparador_maior1_1_maior_a);
endmodule

module Comparador_maior4 (
  input  A0,
  input  I1,
  input  I2,
  input  I3,
  input  B0,
  output out_6
);

  wire comparador_maior1_1_maior_a;

  Comparador_maior1 comparador_maior1_1 (.A(A0), .B(B0), .Maior_A(comparador_maior1_1_maior_a));
  and and_1 (out_6, I1, I2, I3, comparador_maior1_1_maior_a);
endmodule

module Display_a (
  input  [3:0] B,
  output A
);

  wire and_1_out, and_2_out, and_3_out, and_4_out, and_5_out;

  and and_1 (and_1_out, ~B[0], ~B[2]);  // AND_Gate
  and and_2 (and_2_out, B[0], ~B[1], B[3]);  // AND_Gate
  and and_3 (and_3_out, B[0], B[1], ~B[3]);  // AND_Gate
  and and_4 (and_4_out, ~B[1], ~B[2]);  // AND_Gate
  and and_5 (and_5_out, ~B[0], ~B[1], ~B[3]);  // AND_Gate
  or or_1 (A, and_1_out, and_2_out, and_3_out, and_4_out, and_5_out);

  // Notes on the sheet:
  //   D
  //   C
  //   A
  //   -B-D + A-CD + -ACD + -B-C + -A-C-D
endmodule

module Display_b (
  input  [3:0] A,
  output out_2
);

  wire and_1_out, and_2_out, and_3_out, and_4_out, and_5_out, and_6_out;

  and and_1 (and_1_out, ~A[0], ~A[2]);  // AND_Gate
  and and_2 (and_2_out, ~A[0], A[3]);  // AND_Gate
  and and_3 (and_3_out, ~A[1], ~A[2], A[3]);  // AND_Gate
  and and_4 (and_4_out, A[0], A[2], ~A[3]);  // AND_Gate
  and and_5 (and_5_out, A[1], ~A[3]);  // AND_Gate
  and and_6 (and_6_out, A[1], A[2]);
  or or_1 (out_2, and_1_out, and_2_out, and_3_out, and_4_out, and_5_out, and_6_out);

  // Notes on the sheet:
  //   D
  //   -b-d + a-d + a-b-c + -abd + -ac + bc 
endmodule

module Display_c (
  input  [3:0] A,
  output out_2
);

  wire and_1_out, and_2_out, and_3_out, and_4_out, and_5_out;

  and and_1 (and_1_out, ~A[1], A[2], ~A[3]);  // AND_Gate
  and and_2 (and_2_out, ~A[0], ~A[1]);  // AND_Gate
  and and_3 (and_3_out, ~A[2], A[3]);  // AND_Gate
  and and_4 (and_4_out, A[1], A[3]);
  and and_5 (and_5_out, ~A[0], A[2]);  // AND_Gate
  or or_1 (out_2, and_1_out, and_2_out, and_3_out, and_4_out, and_5_out);

  // Notes on the sheet:
  //   D
  //   -ab-c + -c-d + a-b + ac + b-d
endmodule

module Display_d (
  input  [3:0] in_1,
  output out_2
);

  wire and_1_out, and_2_out, and_3_out, and_4_out, and_5_out;

  and and_1 (and_1_out, ~in_1[1], in_1[2], ~in_1[3]);  // AND_Gate
  and and_2 (and_2_out, ~in_1[0], in_1[1]);  // AND_Gate
  and and_3 (and_3_out, ~in_1[2], in_1[3]);  // AND_Gate
  and and_4 (and_4_out, in_1[0], in_1[3]);
  and and_5 (and_5_out, in_1[1], ~in_1[2]);  // AND_Gate
  or or_1 (out_2, and_1_out, and_2_out, and_3_out, and_4_out, and_5_out);

  // Notes on the sheet:
  //   D-C + B-A + DA + -CB + -DC-B
  //   -ab-c + c-d + a-b + ad + -bc
  //   -ab-c + c-d + a-b + ad + -b-c
endmodule

module Display_e (
  input  [3:0] in_1,
  output out_2
);

  wire and_1_out, and_2_out, and_3_out, and_4_out;

  and and_1 (and_1_out, ~in_1[0], in_1[1]);  // AND_Gate
  and and_2 (and_2_out, in_1[2], in_1[3]);
  and and_3 (and_3_out, in_1[1], in_1[3]);
  and and_4 (and_4_out, ~in_1[0], ~in_1[2]);  // AND_Gate
  or or_1 (out_2, and_1_out, and_2_out, and_3_out, and_4_out);

  // Notes on the sheet:
  //    c-d + ab + ac + -b-d
endmodule

module Display_f (
  input  [3:0] in_1,
  output out_2
);

  wire and_1_out, and_2_out, and_3_out, and_4_out, and_5_out;

  and and_1 (and_1_out, ~in_1[0], in_1[2], in_1[1]);  // AND_Gate
  and and_2 (and_2_out, in_1[0], in_1[1], ~in_1[2]);  // AND_Gate
  and and_3 (and_3_out, ~in_1[0], ~in_1[2], ~in_1[3]);  // AND_Gate
  and and_4 (and_4_out, in_1[0], ~in_1[1], in_1[2]);  // AND_Gate
  and and_5 (and_5_out, ~in_1[1], in_1[3]);  // AND_Gate
  or or_1 (out_2, and_1_out, and_2_out, and_3_out, and_4_out, and_5_out);

  // Notes on the sheet:
  //   a-c + b-cd + -a-b-d + -bcd + bc-d
endmodule

module Display_g (
  input  [3:0] in_1,
  output out_2
);

  wire and_1_out, and_2_out, and_3_out, and_4_out, and_5_out;

  and and_1 (and_1_out, ~in_1[2], in_1[3]);  // AND_Gate
  and and_2 (and_2_out, in_1[0], ~in_1[1]);  // AND_Gate
  and and_3 (and_3_out, ~in_1[1], ~in_1[3]);  // AND_Gate
  and and_4 (and_4_out, in_1[2], ~in_1[3]);  // AND_Gate
  and and_5 (and_5_out, in_1[0], ~in_1[3]);  // AND_Gate
  or or_1 (out_2, and_1_out, and_2_out, and_3_out, and_4_out, and_5_out);

  // Notes on the sheet:
  //   a-b + -cd + -a-c + -ab + -ad
endmodule

module display (
  input  A,
  input  B,
  input  C,
  input  D,
  input  E,
  input  F,
  input  G
);

  _7_Segment_Display u_7_segment_display_1 (.g(D), .f(C), .a(B), .b(A), .e(E), .d(F), .c(G));  // open: dp
endmodule

module XNOR (
  input  A0,
  input  B0,
  output S0
);

  wire and_1_out, and_2_out;

  and and_1 (and_1_out, ~A0, ~B0);  // AND_Gate
  and and_2 (and_2_out, A0, B0);
  or or_1 (S0, and_1_out, and_2_out);

  // Notes on the sheet:
  //   XNOR
endmodule

module Maior_ou_menor (
  input  [3:0] Secret,
  input  in_2,
  input  [3:0] User,
  output Maior,
  output Menor
);

  wire undriven;

  Comparador_1bit comparador_1bit_1 (.in_1(Secret[3]), .in_2(User[3]));  // open: out_3
  Comparador_1bit comparador_1bit_2 (.in_1(Secret[2]), .in_2(User[2]));  // open: out_3
  Comparador_1bit comparador_1bit_3 (.in_1(Secret[1]), .in_2(User[1]));  // open: out_3
  Comparador_1bit comparador_1bit_4 (.in_1(Secret[0]), .in_2(User[0]));  // open: out_3
  not not_1 (Menor, undriven);
endmodule

module display_dT (
  input  [3:0] in_1,
  output out_2
);

  wire and_1_out, and_2_out, and_3_out, and_4_out, and_5_out;

  and and_1 (and_1_out, ~in_1[0], in_1[1], ~in_1[2]);  // AND_Gate
  and and_2 (and_2_out, ~in_1[1], in_1[2]);  // AND_Gate
  and and_3 (and_3_out, in_1[0], in_1[3]);
  and and_4 (and_4_out, in_1[2], ~in_1[3]);  // AND_Gate
  and and_5 (and_5_out, ~in_1[0], in_1[1]);  // AND_Gate
  or or_1 (out_2, and_1_out, and_2_out, and_3_out, and_4_out, and_5_out);

  // Notes on the sheet:
  //   D-C + B-A + DA + -CB + -DC-B
endmodule
