// Logisim project Projeto1_circuito.circ as structural Verilog: 13 circuits, main circuit main
module main (
  input  A3,
  input  A2,
  input  A1,
  input  A0,
  input  S,
  input  B3,
  input  B2,
  input  B1,
  input  B0
);

  wire comparador_1_out_2, comparador_1_out_3, comparador_1_out_4, display_intermediario_1_a,
       display_intermediario_1_b, display_intermediario_1_c, display_intermediario_1_d,
       display_intermediario_1_e, display_intermediario_1_f, display_intermediario_1_g,
       display_intermediario_2_a, display_intermediario_2_b, display_intermediario_2_c,
       display_intermediario_2_d, display_intermediario_2_e, display_intermediario_2_f,
       display_intermediario_2_g;
  wire [3:0] seletor_4_bits_personalizado_1_a, seletor_4_bits_personalizado_1_b,
       seletor_4_bits_personalizado_1_c;

  _7_Segment_Display u_7_segment_display_1 (
    .g(display_intermediario_1_d), .f(display_intermediario_1_c), .a(display_intermediario_1_b),
    .b(display_intermediario_1_a), .e(display_intermediario_1_e), .d(display_intermediario_1_f),
    .c(display_intermediario_1_g));  // open: dp
  _7_Segment_Display u_7_segment_display_2 (
    .g(display_intermediario_2_d), .f(display_intermediario_2_c), .a(display_intermediario_2_b),
    .b(display_intermediario_2_a), .e(display_intermediario_2_e), .d(display_intermediario_2_f),
    .c(display_intermediario_2_g));  // open: dp
  Display_intermediario display_intermediario_1 (
    .in_1(seletor_4_bits_personalizado_1_a), .A(display_intermediario_1_a), .B(display_intermediario_1_b),
    .C(display_intermediario_1_c), .D(display_intermediario_1_d), .E(display_intermediario_1_e),
    .F(display_intermediario_1_f), .G(display_intermediario_1_g));
  Display_intermediario display_intermediario_2 (
    .in_1(seletor_4_bits_personalizado_1_b), .A(display_intermediario_2_a), .B(display_intermediario_2_b),
    .C(display_intermediario_2_c), .D(display_intermediario_2_d), .E(display_intermediario_2_e),
    .F(display_intermediario_2_f), .G(display_intermediario_2_g));
  Seletor_4_bits_personalizado seletor_4_bits_personalizado_1 (
    .A(seletor_4_bits_personalizado_1_a), .S(S), .B(seletor_4_bits_personalizado_1_b), .A3(A3), .A2(A2),
    .A1(A1), .A0(A0), .B3(B3), .B2(B2), .B1(B1), .B0(B0), .C(seletor_4_bits_personalizado_1_c));
  Comparador comparador_1 (
    .in_1(seletor_4_bits_personalizado_1_c), .out_2(comparador_1_out_2), .out_3(comparador_1_out_3),
    .out_4(comparador_1_out_4));
  LED Maior (.in(comparador_1_out_2));
  LED Igual (.in(comparador_1_out_3));
  LED Menor (.in(comparador_1_out_4));

  // Notes on the sheet:
  //   Projeto
endmodule

module Seletor (
  input  A,
  input  S,
  input  B,
  output C
);

  wire and_1_out, and_2_out, not_1_out;

  not not_1 (not_1_out, S);
  and and_1 (and_1_out, A, not_1_out);
  and and_2 (and_2_out, S, B);
  or or_1 (C, and_1_out, and_2_out);

  // Notes on the sheet:
  //   Seletor otimizado
endmodule

module Seletor_4_bits (
  input  A0,
  input  B0,
  input  A1,
  input  B1,
  input  S,
  input  A2,
  input  B2,
  input  A3,
  input  B3,
  output [3:0] C
);

  Seletor seletor_1 (.A(A0), .S(S), .B(B0), .C(C[0]));
  Seletor seletor_2 (.A(A1), .S(S), .B(B1), .C(C[1]));
  Seletor seletor_3 (.A(A2), .S(S), .B(B2), .C(C[2]));
  Seletor seletor_4 (.A(A3), .S(S), .B(B3), .C(C[3]));

  // Notes on the sheet:
  //   Seletor_Simples
endmodule

module Seletor_4_bits_personalizado (
  input  A0,
  input  B0,
  input  A1,
  input  B1,
  input  S,
  input  A2,
  input  B2,
  input  A3,
  input  B3,
  output [3:0] A,
  output [3:0] C,
  output [3:0] B
);

  Seletor seletor_1 (.A(A0), .S(S), .B(B0), .C(C[0]));
  Seletor seletor_2 (.A(A1), .S(S), .B(B1), .C(C[1]));
  Seletor seletor_3 (.A(A2), .S(S), .B(B2), .C(C[2]));
  Seletor seletor_4 (.A(A3), .S(S), .B(B3), .C(C[3]));

  assign A = {A3, A2, A1, A0};
  assign B = {B3, B2, B1, B0};

  // Notes on the sheet:
  //   Seletor_Personalizado
endmodule

module Comparador (
  input  [3:0] in_1,
  output out_2,
  output out_3,
  output out_4
);
endmodule

module Display_intermediario (
  input  [3:0] in_1,
  output A,
  output B,
  output C,
  output D,
  output E,
  output F,
  output G
);

  Display_a display_a_1 (.in_1(in_1), .A(A));
  Display_b display_b_1 (.A(in_1), .out_2(B));
  Display_c display_c_1 (.in_1(in_1), .out_2(C));
  Display_d display_d_1 (.in_1(in_1), .out_2(D));
  Display_e display_e_1 (.in_1(in_1), .out_2(E));
  Display_f display_f_1 (.in_1(in_1), .out_2(F));
  Display_g display_g_1 (.in_1(in_1), .out_2(G));

  // Notes on the sheet:
  //   Display Intermediário
endmodule

module Display_a (
  input  [3:0] in_1,
  output A
);

  wire and_1_out, and_2_out, and_3_out, and_4_out, and_5_out;

  and and_1 (and_1_out, ~in_1[0], ~in_1[2]);  // AND_Gate
  and and_2 (and_2_out, in_1[0], ~in_1[1], in_1[3]);  // AND_Gate
  and and_3 (and_3_out, in_1[0], in_1[1], ~in_1[3]);  // AND_Gate
  and and_4 (and_4_out, ~in_1[1], ~in_1[2]);  // AND_Gate
  and and_5 (and_5_out, ~in_1[0], ~in_1[1], ~in_1[3]);  // AND_Gate
  or or_1 (A, and_1_out, and_2_out, and_3_out, and_4_out, and_5_out);

  // Notes on the sheet:
  //   -B-D + A-CD + -ACD + -B-C + -A-C-D
  //   D
  //   C
  //   B
  //   A
  //   -B-C
endmodule

module Display_b (
  input  [3:0] A,
  output out_2
);

  wire and_1_out, and_2_out, and_3_out, and_4_out, and_5_out, and_6_out;

  and and_1 (and_1_out, A[1], ~A[3]);  // AND_Gate
  and and_2 (and_2_out, ~A[1], ~A[2], A[3]);  // AND_Gate
  and and_3 (and_3_out, A[0], A[2], ~A[3]);  // AND_Gate
  and and_4 (and_4_out, ~A[0], ~A[1], ~A[2]);  // AND_Gate
  and and_5 (and_5_out, ~A[0], A[3]);  // AND_Gate
  and and_6 (and_6_out, A[1], A[2], A[3]);
  or or_1 (out_2, and_2_out, and_4_out, and_5_out, and_6_out, and_3_out, and_1_out);

  // Notes on the sheet:
  //   -AC + -ABD + ABC + A-D + -B-C-D + A-B-C
  //   D
  //   C
  //   B
endmodule

module Display_c (
  input  [3:0] in_1,
  output out_2
);

  // OR_Gate or_1 has open pins: out=out_2

  // Notes on the sheet:
  //   -C-D + -AB-C + A-B + AC + B-D
endmodule

module Display_d (
  input  [3:0] in_1,
  output out_2
);

  // OR_Gate or_1 has open pins: out=out_2
endmodule

module Display_e (
  input  [3:0] in_1,
  output out_2
);

  // OR_Gate or_1 has open pins: out=out_2
endmodule

module Display_f (
  input  [3:0] in_1,
  output out_2
);

  // OR_Gate or_1 has open pins: out=out_2
endmodule

module Display_g (
  input  [3:0] in_1,
  output out_2
);

  // OR_Gate or_1 has open pins: out=out_2
endmodule
