// Logisim project projeto 2.circ as structural Verilog
module Flip_Flop_D_subida (
  input  D,
  output Q,
  output nQ
);

  wire CLK_out, nand_1_out, nand_2_out;

  Clock CLK (.out(CLK_out));
  nand nand_1 (nand_1_out, D, CLK_out);
  nand nand_2 (nand_2_out, CLK_out, ~D);  // NAND_Gate
  nand nand_3 (Q, nand_1_out, nQ);
  nand nand_4 (nQ, Q, nand_2_out);

  // Notes on the sheet:
  //   O flip flop tipo D serve para guardar um valor.
endmodule

module \Contador_de_9_à_0  (
  input  CLOCK,
  input  CLEAR,
  input  ENABLE,
  output [3:0] out_4,
  output [3:0] out_5
);

  wire \Circuito_9_à_0_s0 , \Circuito_9_à_0_s1 , \Circuito_9_à_0_s2 , \Circuito_9_à_0_s3 ;

  D_Flip_Flop d_ff_1 (
    .clk(CLOCK), .D(\Circuito_9_à_0_s3 ), .Q(out_4[3]), .Qn(out_5[3]), .en(ENABLE), .reset(CLEAR));  // open: preset
  D_Flip_Flop d_ff_2 (
    .clk(CLOCK), .D(\Circuito_9_à_0_s2 ), .Q(out_4[2]), .Qn(out_5[2]), .en(ENABLE), .reset(CLEAR));  // open: preset
  \Circuito_de_9_à_0  \Circuito_9_à_0  (
    .Q3(out_4[3]), .Q2(out_4[2]), .Q1(out_4[1]), .Q0(out_4[0]), .S3(\Circuito_9_à_0_s3 ),
    .S2(\Circuito_9_à_0_s2 ), .S1(\Circuito_9_à_0_s1 ), .S0(\Circuito_9_à_0_s0 ));
  D_Flip_Flop d_ff_3 (
    .clk(CLOCK), .D(\Circuito_9_à_0_s1 ), .Q(out_4[1]), .Qn(out_5[1]), .en(ENABLE), .reset(CLEAR));  // open: preset
  D_Flip_Flop d_ff_4 (
    .clk(CLOCK), .D(\Circuito_9_à_0_s0 ), .Q(out_4[0]), .Qn(out_5[0]), .en(ENABLE), .reset(CLEAR));  // open: preset
  Hex_Digit_Display hex_digit_display_1 (.value(out_4));  // open: dp
endmodule

module \Circuito_de_9_à_0  (
  input  Q3,
  input  Q2,
  input  Q1,
  input  Q0,
  output S3,
  output S2,
  output S1,
  output S0
);

  wire and_1_out, and_2_out, and_3_out, and_4_out, and_5_out, and_6_out, and_7_out, and_8_out, and_9_out,
       not_1_out, not_2_out, not_3_out, not_4_out, not_5_out, not_6_out, not_7_out, not_8_out, not_9_out,
       not_10_out;

  not not_1 (not_1_out, Q3);
  not not_2 (not_2_out, Q2);
  not not_3 (not_3_out, Q1);
  not not_4 (not_4_out, Q0);
  not not_5 (not_5_out, Q1);
  not not_6 (not_6_out, Q0);
  not not_7 (not_7_out, Q1);
  not not_8 (not_8_out, Q0);
  not not_9 (not_9_out, Q1);
  not not_10 (not_10_out, Q0);
  not not_11 (S0, Q0);
  and and_1 (and_1_out, not_1_out, not_2_out, not_3_out, not_4_out);
  and and_2 (and_2_out, Q3, Q0);
  and and_3 (and_3_out, Q3, Q1);
  and and_4 (and_4_out, Q2, Q0);
  and and_5 (and_5_out, Q2, Q1);
  and and_6 (and_6_out, Q3, not_5_out, not_6_out);
  and and_7 (and_7_out, Q1, Q0);
  and and_8 (and_8_out, Q2, not_7_out, not_8_out);
  and and_9 (and_9_out, Q3, not_9_out, not_10_out);
  or or_1 (S3, and_1_out, and_2_out, and_3_out);
  or or_2 (S2, and_4_out, and_5_out, and_6_out);
  or or_3 (S1, and_7_out, and_8_out, and_9_out);
  // AND_Gate and_10 is placed but not wired

  // Notes on the sheet:
  //   Circuito para usar no contador de 0 à 9
endmodule
