// Logisim project projeto de circuito 2.circ as structural Verilog: 31 circuits, main circuit main
module main (
  input  in_1,
  input  in_2,
  input  in_3,
  input  in_4,
  input  in_5,
  input  in_6,
  input  in_7,
  input  in_8,
  input  in_9,
  input  in_10
);

  wire A_jogando, A_Venceu, Acertou, B_jogando, B_Venceu, Chutando_X, Chutando_Y, Chutar, configurar,
       converte5para4_1_out_3, converte5para4_2_out_3, dma_t, dmb_t, dsa_t, dsb_t, Empate, Fim_de_Jogo,
       Igual, Maior, Menor, ON, ON_OFF, Proximo, reset, SA, SB, SX, SY, tunnel, uma_t, umb_t, usa_t, usb_t;
  wire [3:0] converte5para4_1_out_2, converte5para4_2_out_2, DMA, DMB, DSA, DSB, GA, GB, PA, PB, UMA, UMB,
       USA, USB, XH, YH;
  wire [4:0] jogo_1_out_32, jogo_1_out_36;

  Button button_1 (.out(dma_t));
  Hex_Digit_Display hex_digit_display_1 (.value(DMA));  // open: dp
  Hex_Digit_Display hex_digit_display_2 (.value(PA));  // open: dp
  Button button_2 (.out(uma_t));
  LED led_1 (.in(1'b1));
  LED led_2 (.in(1'b1));
  Hex_Digit_Display hex_digit_display_3 (.value(UMA));  // open: dp
  LED led_3 (.in(SA));
  Hex_Digit_Display hex_digit_display_4 (.value(GA));  // open: dp
  LED led_4 (.in(A_jogando));
  Button button_3 (.out(dsa_t));
  Button button_4 (.out(usa_t));
  Hex_Digit_Display hex_digit_display_5 (.value(DSA));  // open: dp
  Hex_Digit_Display hex_digit_display_6 (.value(USA));  // open: dp
  LED led_5 (.in(A_Venceu));
  LED led_6 (.in(ON));
  Button button_5 (.out(ON_OFF));
  LED led_7 (.in(Maior));
  LED led_8 (.in(SX));
  Hex_Digit_Display hex_digit_display_7 (.value(XH));  // open: dp
  LED led_9 (.in(Chutando_X));
  LED led_10 (.in(Fim_de_Jogo));
  LED led_11 (.in(Empate));
  LED led_12 (.in(tunnel));
  Button button_6 (.out(configurar));
  LED led_13 (.in(Acertou));
  LED led_14 (.in(Igual));
  Button button_7 (.out(Proximo));
  LED led_15 (.in(B_Venceu));
  Button button_8 (.out(reset));
  LED led_16 (.in(Menor));
  Button button_9 (.out(Chutar));
  Hex_Digit_Display hex_digit_display_8 (.value(YH));  // open: dp
  LED led_17 (.in(SY));
  LED led_18 (.in(Chutando_Y));
  Button button_10 (.out(umb_t));
  Button button_11 (.out(dmb_t));
  Hex_Digit_Display hex_digit_display_9 (.value(UMB));  // open: dp
  Hex_Digit_Display hex_digit_display_10 (.value(DMB));  // open: dp
  Hex_Digit_Display hex_digit_display_11 (.value(PB));  // open: dp
  LED led_19 (.in(1'b1));
  LED led_20 (.in(1'b1));
  Hex_Digit_Display hex_digit_display_12 (.value(DSB));  // open: dp
  Hex_Digit_Display hex_digit_display_13 (.value(GB));  // open: dp
  LED led_21 (.in(SB));
  LED led_22 (.in(B_jogando));
  Button button_12 (.out(usb_t));
  Button button_13 (.out(dsb_t));
  Hex_Digit_Display hex_digit_display_14 (.value(USB));  // open: dp
  Jogo jogo_1 (
    .SA_2(SA), .numeroA_2(GA), .Jogador_A_chutando(A_jogando), .SA(SX), .numeroA(XH), .SB1(SY), .numeroB(YH),
    .Jogador_B_chutando(B_jogando), .SB2(SB), .numeroB_2(GB), .S_2(in_6), .A3(in_7), .A2(in_8), .A1(in_9),
    .A0(in_10), .S(in_1), .B3(in_2), .B2(in_3), .B1(in_4), .B0(in_5), .Coordenada_X(Chutando_X),
    .Coordenada_Y(Chutando_Y), .Start(ON_OFF), .Acertou(Acertou), .Igual(Igual), .Maior(Maior),
    .Menor(Menor), .out_32(jogo_1_out_32), .out_36(jogo_1_out_36), .out_50(DMB), .out_52(UMB), .out_55(DSB),
    .out_57(USB), .out_49(DMA), .out_51(UMA), .out_54(DSA), .out_56(USA), .usa(usa_t), .dsa_2(dsa_t),
    .uma(uma_t), .dma(dma_t), .mod(configurar), .usb(usb_t), .dsa(dsb_t), .umb(umb_t), .dmb(dmb_t),
    .Configure(tunnel), .VenceuA(A_Venceu), .VenceuB(B_Venceu), .Empate(Empate), .Fim_do_jogo(Fim_de_Jogo),
    .Placar_A(PA), .ON_OFF(ON), .Proximo(Proximo), .Chute(Chutar), .Placar_B(PB), .reset(reset));
  LED led_23 (.in(converte5para4_1_out_3));
  Hex_Digit_Display hex_digit_display_15 (.value(converte5para4_1_out_2));  // open: dp
  converte5para4 converte5para4_1 (
    .out_3(converte5para4_1_out_3), .in_1(jogo_1_out_32), .out_2(converte5para4_1_out_2));
  converte5para4 converte5para4_2 (
    .out_3(converte5para4_2_out_3), .in_1(jogo_1_out_36), .out_2(converte5para4_2_out_2));
  LED led_24 (.in(converte5para4_2_out_3));
  Hex_Digit_Display hex_digit_display_16 (.value(converte5para4_2_out_2));  // open: dp

  // Other names for the same wires on the sheet: A0 = in_10; A1 = in_9; A2 = in_8; A3 = in_7; A4 = in_6; B0 = in_5;
  //   B1 = in_4; B2 = in_3; B3 = in_2; B4 = in_1

  // Notes on the sheet:
  //   Jogador A
  //   Jogador A
  //   Jogador B
  //   Jogador B
endmodule

// JOGO
module Jogo (
  input  Start,
  input  reset,
  input  Chute,
  input  Proximo,
  input  S,
  input  B3,
  input  B2,
  input  B1,
  input  B0,
  input  S_2,
  input  A3,
  input  A2,
  input  A1,
  input  A0,
  input  mod,
  input  usa,
  input  usb,
  input  dsa,
  input  dsa_2,
  input  umb,
  input  uma,
  input  dmb,
  input  dma,
  output VenceuA,
  output VenceuB,
  output [3:0] Placar_B,
  output [3:0] Placar_A,
  output Empate,
  output Fim_do_jogo,
  output ON_OFF,
  output Acertou,
  output [4:0] out_32,
  output Igual,
  output Maior,
  output Menor,
  output [4:0] out_36,
  output Jogador_A_chutando,
  output Coordenada_X,
  output Jogador_B_chutando,
  output Coordenada_Y,
  output SA,
  output [3:0] numeroA,
  output SB1,
  output [3:0] numeroB,
  output SB2,
  output [3:0] numeroB_2,
  output SA_2,
  output [3:0] numeroA_2,
  output [3:0] out_49,
  output [3:0] out_50,
  output [3:0] out_51,
  output [3:0] out_52,
  output Configure,
  output [3:0] out_54,
  output [3:0] out_55,
  output [3:0] out_56,
  output [3:0] out_57
);

  wire A_jogando, acertou_t, analisador_1_igual, analisador_1_maior, analisador_1_menor, and_10_out,
       and_11_out, Chute_Y_ON, Clock, clock_1_out, converte5para4_1_out_3, converte5para4_2_out_3,
       converte5para4_3_out_3, converte5para4_4_out_3, FimA, FimB, IGUALA, IGUALB, mod_1_out_2, Mod_t,
       not_3_out, not_4_out, not_5_out, or_2_out, or_3_out, or_4_out, Placar_Igual;
  wire [3:0] converte5para4_1_out_2, converte5para4_2_out_2, converte5para4_3_out_2, converte5para4_4_out_2;
  wire [4:0] numerouser_1_s, numerouseroeste_1_s;

  LED led_1 (.in(converte5para4_1_out_3));
  and and_1 (VenceuA, IGUALA, ~IGUALB);  // AND_Gate
  and and_2 (VenceuB, ~IGUALA, IGUALB);  // AND_Gate
  and and_3 (Empate, FimA, FimB, Placar_Igual);
  or or_1 (Fim_do_jogo, VenceuB, Empate, VenceuA);
  Hex_Digit_Display hex_digit_display_1 (.value(converte5para4_1_out_2));  // open: dp
  converte5para4 converte5para4_1 (
    .out_3(converte5para4_1_out_3), .in_1({SA, numeroA}), .out_2(converte5para4_1_out_2));
  mod mod_1 (.in_1(Start), .out_2(mod_1_out_2));
  Clock clock_1 (.out(clock_1_out));
  NumeroUser numerouser_1 (
    .out_7(SA_2), .out_6(numeroA_2), .in_1(S_2), .in_2(A3), .in_3(A2), .in_4(A1), .in_5(A0),
    .S(numerouser_1_s));
  not not_1 (ON_OFF, mod_1_out_2);
  and and_4 (Clock, ON_OFF, clock_1_out);
  Comparator #(.width(4)) comparator_1 (.a(Placar_A), .b(Placar_B), .eq(Placar_Igual));  // open: gt, lt
  Hex_Digit_Display hex_digit_display_2 (.value(converte5para4_2_out_2));  // open: dp
  LED led_2 (.in(converte5para4_2_out_3));
  converte5para4 converte5para4_2 (.out_3(converte5para4_2_out_3), .in_1(out_32), .out_2(converte5para4_2_out_2));
  or or_2 (or_2_out, acertou_t, reset, Start);
  and and_5 (Jogador_A_chutando, ON_OFF, A_jogando);
  not not_2 (A_jogando, Jogador_B_chutando);
  cronometro cronometro_1 (
    .time1(usa), .reset(reset), .time2(dsa_2), .time3(uma), .time4(dma), .mod(Mod_t), .Enable(or_3_out),
    .Clock(Clock), .DM(out_49), .UM(out_51), .DS(out_54), .US(out_56), .Fim_do_tempo(FimA));
  or or_3 (or_3_out, not_3_out, A_jogando);
  not not_3 (not_3_out, Mod_t);
  Random #(.width(5)) random_1 (.clk(or_2_out), .out(out_32));  // open: next, clr
  Random #(.width(5), .seed(8)) random_2 (.clk(or_2_out), .out(out_36));  // open: next, clr
  and and_6 (Coordenada_X, ON_OFF, not_4_out);
  not not_4 (not_4_out, Coordenada_Y);
  LED led_3 (.in(converte5para4_3_out_3));
  Hex_Digit_Display hex_digit_display_3 (.value(converte5para4_3_out_2));  // open: dp
  converte5para4 converte5para4_3 (.out_3(converte5para4_3_out_3), .in_1(out_36), .out_2(converte5para4_3_out_2));
  analisador analisador_1 (
    .X_random(out_32), .Y_random(out_36), .Acertou(acertou_t), .X_user({SA, numeroA}),
    .Y_user({SB1, numeroB}), .Igual(analisador_1_igual), .Maior(analisador_1_maior),
    .Menor(analisador_1_menor));
  placar placar_1 (.Jogador(A_jogando), .Clock(acertou_t), .Clear(reset), .Igual(IGUALA), .Placar(Placar_A));
  and and_7 (Igual, analisador_1_igual, and_10_out);
  and and_8 (Maior, analisador_1_maior, and_10_out);
  and and_9 (Menor, analisador_1_menor, and_10_out);
  and and_10 (and_10_out, ON_OFF, Chute_Y_ON);
  Seletor seletor_1 (
    .A(numerouser_1_s), .in_5(numerouseroeste_1_s), .out_7(numeroA), .out_9(numeroB), .out_6(SA),
    .out_8(SB1), .Proximo(Proximo), .Clock(Clock), .Chute(Chute), .Jogador_A_ou_B(Jogador_B_chutando),
    .Coordenada_X_ou_Y(Coordenada_Y));
  mod mod_2 (.in_1(mod), .out_2(Mod_t));
  cronometro cronometro_2 (
    .time1(usb), .reset(reset), .time2(dsa), .time3(umb), .time4(dmb), .mod(Mod_t), .Enable(or_4_out),
    .Clock(Clock), .DM(out_50), .UM(out_52), .DS(out_55), .US(out_57), .Fim_do_tempo(FimB));
  or or_4 (or_4_out, not_5_out, Jogador_B_chutando);
  not not_5 (not_5_out, Mod_t);
  placar placar_2 (.Jogador(Jogador_B_chutando), .Clock(acertou_t), .Clear(reset), .Igual(IGUALB), .Placar(Placar_B));
  contador_0_a_7 contador_0_a_7_1 (.in_1(acertou_t), .out_2(Acertou));
  Hex_Digit_Display hex_digit_display_4 (.value(converte5para4_4_out_2));  // open: dp
  LED led_4 (.in(converte5para4_4_out_3));
  converte5para4 converte5para4_4 (
    .out_3(converte5para4_4_out_3), .in_1({SB1, numeroB}), .out_2(converte5para4_4_out_2));
  NumeroUserOeste numerouseroeste_1 (
    .S(numerouseroeste_1_s), .out_7(SB2), .out_6(numeroB_2), .in_1(S), .in_2(B3), .in_3(B2), .in_4(B1),
    .in_5(B0));
  not not_6 (Configure, Mod_t);
  and and_11 (and_11_out, Coordenada_Y, Chute);
  contador_0_a_7 contador_0_a_7_2 (.in_1(and_11_out), .out_2(Chute_Y_ON));

  // Other names for the same wires on the sheet: Chute_X = Coordenada_X; Chute_Y = Coordenada_Y; ChuteON = Chute;
  //   DMA_t[3:0] = out_49; DMB_t[3:0] = out_50; DSA_t[3:0] = out_54; DSB[3:0] = out_55; EnableA = A_jogando;
  //   B_jogando = Jogador_B_chutando; EnableB = Jogador_B_chutando; ON = ON_OFF; ProximoON = Proximo; temp1A = usa;
  //   temp1B = usb; temp2A = dsa_2; temp2B = dsa; temp3A = uma; temp3B = umb; temp4A = dma; temp4B = dmb;
  //   UMA_t[3:0] = out_51; UMB_t[3:0] = out_52; USA_t[3:0] = out_56; USB_t[3:0] = out_57
endmodule

module cronometro (
  input  Clock,
  input  time1,
  input  reset,
  input  time2,
  input  time3,
  input  time4,
  input  mod,
  input  Enable,
  output [3:0] DM,
  output [3:0] UM,
  output [3:0] DS,
  output [3:0] US,
  output Fim_do_tempo
);

  wire and_1_out, and_3_out, comparador_de_igual_4_bits_1_igual, comparador_de_igual_4_bits_2_igual,
       comparador_de_igual_4_bits_3_igual, comparador_de_igual_4_bits_4_igual,
       \contador_de_5_à_0_dezena_dos_minutos_1_saida_1 , \contador_de_5_à_0_dezena_dos_minutos_1_saida_2 ,
       \contador_de_5_à_0_dezena_dos_minutos_1_saida_3 , \contador_de_5_à_0_dezena_dos_minutos_1_sinal_de_0 ,
       \contador_de_5_à_0_dezena_dos_minutos_2_sinal_de_0 , \contador_de_9_à_0_unidade_seg_e_min_1_out_8 ,
       \contador_de_9_à_0_unidade_seg_e_min_1_out_9 , \contador_de_9_à_0_unidade_seg_e_min_1_out_10 ,
       \contador_de_9_à_0_unidade_seg_e_min_1_out_11 , \contador_de_9_à_0_unidade_seg_e_min_1_saida_de_0 ,
       \copia_do_0_à_9_unidade_de_minutos_1_saida_0 , \copia_do_0_à_9_unidade_de_minutos_1_saida_1 ,
       \copia_do_0_à_9_unidade_de_minutos_1_saida_2 , \copia_do_0_à_9_unidade_de_minutos_1_saida_3 ,
       \copia_do_0_à_9_unidade_de_minutos_1_saida_de_0 ;

  and and_1 (and_1_out, Enable, ~and_3_out);  // AND_Gate
  \Contador_de_9_à_0_unidade_seg_e_min  \contador_de_9_à_0_unidade_seg_e_min_1  (
    .CLOCK(Clock), .tempo(time1), .MOD(mod), .out_7(US),
    .out_8(\contador_de_9_à_0_unidade_seg_e_min_1_out_8 ),
    .out_9(\contador_de_9_à_0_unidade_seg_e_min_1_out_9 ),
    .out_10(\contador_de_9_à_0_unidade_seg_e_min_1_out_10 ),
    .out_11(\contador_de_9_à_0_unidade_seg_e_min_1_out_11 ), .ENABLE(and_1_out), .CLEAR(reset),
    .saida_de_0(\contador_de_9_à_0_unidade_seg_e_min_1_saida_de_0 ));
  \Contador_de_5_à_0_dezena_dos_minutos  \contador_de_5_à_0_dezena_dos_minutos_1  (
    .CLK(\contador_de_9_à_0_unidade_seg_e_min_1_out_11 ),
    .CLK_2(\contador_de_9_à_0_unidade_seg_e_min_1_out_8 ),
    .CLK_3(\contador_de_9_à_0_unidade_seg_e_min_1_out_9 ),
    .CLOCK(\contador_de_9_à_0_unidade_seg_e_min_1_out_10 ), .tempo(time2), .MOD(mod), .Clear(reset),
    .out_10(DS), .SAIDA_3(\contador_de_5_à_0_dezena_dos_minutos_1_saida_3 ),
    .SAIDA_2(\contador_de_5_à_0_dezena_dos_minutos_1_saida_2 ),
    .SAIDA_1(\contador_de_5_à_0_dezena_dos_minutos_1_saida_1 ), .enable(and_1_out),
    .Sinal_de_0(\contador_de_5_à_0_dezena_dos_minutos_1_sinal_de_0 ));
  \Copia_do_0_à_9_unidade_de_minutos  \copia_do_0_à_9_unidade_de_minutos_1  (
    .CLK(\contador_de_5_à_0_dezena_dos_minutos_1_saida_3 ),
    .CLK_2(\contador_de_5_à_0_dezena_dos_minutos_1_saida_2 ),
    .CLOCK(\contador_de_5_à_0_dezena_dos_minutos_1_saida_1 ), .tempo(time3), .MOD(mod), .ENABLE(and_1_out),
    .CLEAR(reset), .saida_de_0(\copia_do_0_à_9_unidade_de_minutos_1_saida_de_0 ), .out_9(UM),
    .SAIDA_3(\copia_do_0_à_9_unidade_de_minutos_1_saida_3 ),
    .SAIDA_2(\copia_do_0_à_9_unidade_de_minutos_1_saida_2 ),
    .SAIDA_1(\copia_do_0_à_9_unidade_de_minutos_1_saida_1 ),
    .SAIDA_0(\copia_do_0_à_9_unidade_de_minutos_1_saida_0 ));
  \Contador_de_5_à_0_dezena_dos_minutos  \contador_de_5_à_0_dezena_dos_minutos_2  (
    .CLK(\copia_do_0_à_9_unidade_de_minutos_1_saida_0 ),
    .CLK_2(\copia_do_0_à_9_unidade_de_minutos_1_saida_3 ),
    .CLK_3(\copia_do_0_à_9_unidade_de_minutos_1_saida_2 ),
    .CLOCK(\copia_do_0_à_9_unidade_de_minutos_1_saida_1 ), .tempo(time4), .MOD(mod), .Clear(reset),
    .out_10(DM), .enable(and_1_out), .Sinal_de_0(\contador_de_5_à_0_dezena_dos_minutos_2_sinal_de_0 ));  // open: SAIDA_3, SAIDA_2, SAIDA_1
  comparador_de_igual_4_bits comparador_de_igual_4_bits_1 (
    .A(4'b0000), .B(DM), .Igual(comparador_de_igual_4_bits_1_igual));
  comparador_de_igual_4_bits comparador_de_igual_4_bits_2 (
    .A(4'b0000), .B(UM), .Igual(comparador_de_igual_4_bits_2_igual));
  and and_2 (Fim_do_tempo, comparador_de_igual_4_bits_1_igual, comparador_de_igual_4_bits_2_igual, comparador_de_igual_4_bits_3_igual, comparador_de_igual_4_bits_4_igual);
  and and_3 (and_3_out, \contador_de_5_à_0_dezena_dos_minutos_2_sinal_de_0 , \copia_do_0_à_9_unidade_de_minutos_1_saida_de_0 , \contador_de_5_à_0_dezena_dos_minutos_1_sinal_de_0 , \contador_de_9_à_0_unidade_seg_e_min_1_saida_de_0 );
  comparador_de_igual_4_bits comparador_de_igual_4_bits_3 (
    .A(4'b0000), .B(DS), .Igual(comparador_de_igual_4_bits_3_igual));
  comparador_de_igual_4_bits comparador_de_igual_4_bits_4 (
    .A(4'b0000), .B(US), .Igual(comparador_de_igual_4_bits_4_igual));
endmodule

module NumeroUser (
  input  in_1,
  input  in_2,
  input  in_3,
  input  in_4,
  input  in_5,
  output [3:0] out_6,
  output out_7,
  output [4:0] S
);


  assign out_6 = {in_2, in_3, in_4, in_5};
  assign out_7 = in_1;
  assign S = {in_1, in_2, in_3, in_4, in_5};
endmodule

// NumeroUser
module NumeroUserOeste (
  input  in_1,
  input  in_2,
  input  in_3,
  input  in_4,
  input  in_5,
  output [3:0] out_6,
  output out_7,
  output [4:0] S
);


  assign out_6 = {in_2, in_3, in_4, in_5};
  assign out_7 = in_1;
  assign S = {in_1, in_2, in_3, in_4, in_5};
endmodule

module Seletor (
  input  Chute,
  input  Clock,
  input  Proximo,
  input  [4:0] A,
  input  [4:0] in_5,
  output out_6,
  output [3:0] out_7,
  output out_8,
  output [3:0] out_9,
  output Coordenada_X_ou_Y,
  output Jogador_A_ou_B
);

  wire chute_1_x, chute_1_y;
  wire [4:0] demultiplexer_1_out0, demultiplexer_1_out1, multiplexer_1_out, register_1_q, register_2_q;

  chute chute_1 (.Chute(Chute), .X_ou_Y(Coordenada_X_ou_Y), .X(chute_1_x), .Y(chute_1_y));
  proximo proximo_1 (.Proximo(Proximo), .Clock(Clock), .X_ou_Y(Coordenada_X_ou_Y), .A_ou_B(Jogador_A_ou_B));
  converte5para4 converte5para4_1 (.out_3(out_6), .in_1(register_1_q), .out_2(out_7));
  Register #(.width(5)) register_1 (.D(demultiplexer_1_out0), .Q(register_1_q), .clk(chute_1_x));  // open: en, clr
  Demultiplexer #(.width(5), .enable("false")) demultiplexer_1 (
    .out0(demultiplexer_1_out0), .out1(demultiplexer_1_out1), .in(multiplexer_1_out), .sel(Coordenada_X_ou_Y));
  Multiplexer #(.width(5), .enable("false")) multiplexer_1 (
    .in0(A), .in1(in_5), .out(multiplexer_1_out), .sel(Jogador_A_ou_B));
  converte5para4 converte5para4_2 (.out_3(out_8), .in_1(register_2_q), .out_2(out_9));
  Register #(.width(5)) register_2 (.D(demultiplexer_1_out1), .Q(register_2_q), .clk(chute_1_y));  // open: en, clr
endmodule

module RandomNumber (
  input  Clock,
  output [4:0] out_2,
  output [4:0] out_3
);

  wire converte5para4_1_out_3, converte5para4_2_out_3;
  wire [3:0] converte5para4_1_out_2, converte5para4_2_out_2;

  LED led_1 (.in(converte5para4_2_out_3));
  LED led_2 (.in(converte5para4_1_out_3));
  Hex_Digit_Display hex_digit_display_1 (.value(converte5para4_1_out_2));  // open: dp
  converte5para4 converte5para4_1 (.out_3(converte5para4_1_out_3), .in_1(out_2), .out_2(converte5para4_1_out_2));
  Random #(.width(5)) random_1 (.clk(Clock), .out(out_2));  // open: next, clr
  Random #(.width(5), .seed(70909)) random_2 (.clk(Clock), .out(out_3));  // open: next, clr
  converte5para4 converte5para4_2 (.out_3(converte5para4_2_out_3), .in_1(out_3), .out_2(converte5para4_2_out_2));
  Hex_Digit_Display hex_digit_display_2 (.value(converte5para4_2_out_2));  // open: dp
endmodule

module converte5para4 (
  input  [4:0] in_1,
  output [3:0] out_2,
  output out_3
);


  assign out_2 = in_1[3:0];
  assign out_3 = in_1[4];
endmodule

module proximo (
  input  Clock,
  input  Proximo,
  output X_ou_Y,
  output A_ou_B
);

  wire and_1_out, and_2_out, and_3_out, and_4_out, and_5_out, and_6_out, and_7_out, and_8_out, or_1_out,
       or_2_out;

  and and_1 (and_1_out, Proximo, ~X_ou_Y, ~A_ou_B);  // AND_Gate
  and and_2 (and_2_out, ~Proximo, X_ou_Y, ~A_ou_B);  // AND_Gate
  and and_3 (and_3_out, Proximo, ~X_ou_Y, A_ou_B);  // AND_Gate
  and and_4 (and_4_out, ~Proximo, X_ou_Y, A_ou_B);  // AND_Gate
  and and_5 (and_5_out, Proximo, X_ou_Y, ~A_ou_B);  // AND_Gate
  and and_6 (and_6_out, ~Proximo, ~X_ou_Y, A_ou_B);  // AND_Gate
  and and_7 (and_7_out, Proximo, ~X_ou_Y, A_ou_B);  // AND_Gate
  and and_8 (and_8_out, ~Proximo, X_ou_Y, A_ou_B);  // AND_Gate
  or or_1 (or_1_out, and_1_out, and_2_out, and_3_out, and_4_out);
  or or_2 (or_2_out, and_5_out, and_6_out, and_7_out, and_8_out);
  D_Flip_Flop d_ff_1 (.clk(Clock), .D(or_1_out), .Q(X_ou_Y));  // open: Qn, preset, en, reset
  D_Flip_Flop d_ff_2 (.clk(Clock), .D(or_2_out), .Q(A_ou_B));  // open: Qn, preset, en, reset
endmodule

module chute (
  input  Chute,
  input  X_ou_Y,
  output X,
  output Y
);

  and and_1 (X, Chute, ~X_ou_Y);  // AND_Gate
  and and_2 (Y, Chute, X_ou_Y);
endmodule

module analisador (
  input  [4:0] X_random,
  input  [4:0] Y_random,
  input  [4:0] X_user,
  input  [4:0] Y_user,
  output Acertou,
  output Igual,
  output Maior,
  output Menor
);

  wire comparadordeigualdade_1_igual, comparadordeigualdade_2_igual;
  wire [5:0] somador_2_out_3, Somador_out_3;

  Somador Somador (.X(X_random), .Y(Y_random), .out_3(Somador_out_3));
  comparadorDeIgualdade comparadordeigualdade_1 (.A(X_random), .B(X_user), .Igual(comparadordeigualdade_1_igual));
  Somador somador_2 (.X(X_user), .Y(Y_user), .out_3(somador_2_out_3));
  and and_1 (Acertou, comparadordeigualdade_1_igual, comparadordeigualdade_2_igual, Igual);
  comparador comparador_1 (.A(Somador_out_3), .B(somador_2_out_3), .Igual(Igual), .Maior(Maior), .Menor(Menor));
  comparadorDeIgualdade comparadordeigualdade_2 (.A(Y_random), .B(Y_user), .Igual(comparadordeigualdade_2_igual));
endmodule

module Somador (
  input  [4:0] X,
  input  [4:0] Y,
  output [5:0] out_3
);

  wire [1:0] Converte5_para_4_1_out_3;
  wire [3:0] adder_1_out, adder_2_out, adder_3_out, adder_4_out, Converte5_para_4_1_2_out_2,
       Converte5_para_4_1_out_2, multiplexer_1_out, multiplexer_2_out, negator_1_out, negator_2_out,
       negator_3_out, negator_4_out;
  wire [4:4] adder_1_cout, adder_4_cout;
  wire [5:5] comparator_1_lt, not_1_out;

  converte5para4 Converte5_para_4_1 (.out_3(Converte5_para_4_1_out_3[0]), .in_1(X), .out_2(Converte5_para_4_1_out_2));
  converte5para4 Converte5_para_4_1_2 (
    .out_3(Converte5_para_4_1_out_3[1]), .in_1(Y), .out_2(Converte5_para_4_1_2_out_2));
  Negator #(.width(4)) negator_1 (.in(Converte5_para_4_1_out_2), .out(negator_1_out));
  Negator #(.width(4)) negator_2 (.in(Converte5_para_4_1_2_out_2), .out(negator_2_out));
  Adder #(.width(4)) adder_1 (
    .a(Converte5_para_4_1_out_2), .b(Converte5_para_4_1_2_out_2), .out(adder_1_out), .cout(adder_1_cout[4]));  // open: cin
  Adder #(.width(4)) adder_2 (.a(negator_1_out), .b(Converte5_para_4_1_2_out_2), .out(adder_2_out));  // open: cin, cout
  Comparator #(.width(4)) comparator_1 (
    .a(Converte5_para_4_1_out_2), .b(Converte5_para_4_1_2_out_2), .lt(comparator_1_lt[5]));  // open: gt, eq
  not not_1 (not_1_out[5], comparator_1_lt[5]);
  Adder #(.width(4)) adder_3 (.a(Converte5_para_4_1_out_2), .b(negator_2_out), .out(adder_3_out));  // open: cin, cout
  Adder #(.width(4)) adder_4 (
    .a(Converte5_para_4_1_out_2), .b(Converte5_para_4_1_2_out_2), .out(adder_4_out), .cout(adder_4_cout[4]));  // open: cin
  Multiplexer #(.width(4), .enable("false")) multiplexer_1 (
    .in0(adder_2_out), .in1(negator_3_out), .out(multiplexer_1_out), .sel(comparator_1_lt[5]));
  Negator #(.width(4)) negator_3 (.in(adder_2_out), .out(negator_3_out));
  Multiplexer #(.width(4), .enable("false")) multiplexer_2 (
    .in0(adder_3_out), .in1(negator_4_out), .out(multiplexer_2_out), .sel(not_1_out[5]));
  Negator #(.width(4)) negator_4 (.in(adder_3_out), .out(negator_4_out));
  Multiplexer #(.select(2), .width(6), .enable("false")) multiplexer_3 (
    .in0({1'b0, adder_1_cout[4], adder_1_out}), .in1({comparator_1_lt[5], 1'b0, multiplexer_1_out}),
    .in2({not_1_out[5], 1'b0, multiplexer_2_out}), .in3({1'b1, adder_4_cout[4], adder_4_out}), .out(out_3),
    .sel(Converte5_para_4_1_out_3));
endmodule

module comparador (
  input  [5:0] A,
  input  [5:0] B,
  output Igual,
  output Maior,
  output Menor
);

  wire and_1_out, and_2_out, and_3_out, and_4_out, and_5_out, and_6_out, and_7_out, and_8_out, and_9_out,
       and_10_out, comparator_1_eq, comparator_1_lt, or_1_out;

  and and_1 (and_1_out, ~1'b0, ~A[0], ~A[1], ~A[2], ~A[3], ~A[4]);  // AND_Gate
  Comparator #(.width(5)) comparator_1 (
    .a(A[4:0]), .b(B[4:0]), .eq(comparator_1_eq), .lt(comparator_1_lt));  // open: gt
  and and_2 (and_2_out, ~1'b0, ~B[0], ~B[1], ~B[2], ~B[3], ~B[4]);  // AND_Gate
  and and_3 (and_3_out, and_1_out, and_2_out);
  and and_4 (and_4_out, A[5], B[5]);
  or or_1 (or_1_out, and_4_out, and_5_out);
  and and_5 (and_5_out, ~A[5], ~B[5]);  // AND_Gate
  and and_6 (and_6_out, comparator_1_eq, or_1_out);
  or or_2 (Igual, and_3_out, and_6_out);
  and and_7 (and_7_out, ~A[5], ~1'b0);  // AND_Gate
  and and_8 (and_8_out, B[5], 1'b1);
  and and_9 (and_9_out, comparator_1_lt, or_1_out);
  and and_10 (and_10_out, and_7_out, ~Igual, and_8_out);  // AND_Gate
  or or_3 (Maior, and_9_out, and_10_out);
  and and_11 (Menor, ~Igual, ~Maior);  // AND_Gate

  // Notes on the sheet:
  //   Verifica se os sinais são iguais
  //   Verifica se os números são zeros
endmodule

module comparadorDeIgualdade (
  input  [4:0] A,
  input  [4:0] B,
  output Igual
);

  wire and_1_out, and_2_out, and_3_out, and_4_out, igual_1_s, igual_2_s, igual_3_s, igual_4_s, igual_5_s;

  and and_1 (and_1_out, ~1'b0, ~A[0], ~A[1], ~A[2], ~A[3]);  // AND_Gate
  Igual igual_1 (.A(A[0]), .B(B[0]), .S(igual_1_s));
  Igual igual_2 (.A(A[1]), .B(B[1]), .S(igual_2_s));
  and and_2 (and_2_out, ~1'b0, ~B[0], ~B[1], ~B[2], ~B[3]);  // AND_Gate
  Igual igual_3 (.A(A[2]), .B(B[2]), .S(igual_3_s));
  Igual igual_4 (.A(A[3]), .B(B[3]), .S(igual_4_s));
  Igual igual_5 (.A(A[4]), .B(B[4]), .S(igual_5_s));
  and and_3 (and_3_out, igual_1_s, igual_2_s, igual_3_s, igual_4_s, igual_5_s);
  and and_4 (and_4_out, and_1_out, and_2_out);
  or or_1 (Igual, and_4_out, and_3_out);
endmodule

module Igual (
  input  A,
  input  B,
  output S
);

  wire and_1_out, and_2_out;

  and and_1 (and_1_out, A, B);
  and and_2 (and_2_out, ~A, ~B);  // AND_Gate
  or or_1 (S, and_1_out, and_2_out);
endmodule

module mod (
  input  in_1,
  output out_2
);

  wire and_1_out, and_2_out, clock_1_out, d_ff_1_q, or_1_out;

  and and_1 (and_1_out, ~in_1, d_ff_1_q);  // AND_Gate
  and and_2 (and_2_out, in_1, ~d_ff_1_q);  // AND_Gate
  or or_1 (or_1_out, and_2_out, and_1_out);
  Clock clock_1 (.out(clock_1_out));
  D_Flip_Flop d_ff_1 (.clk(clock_1_out), .D(or_1_out), .Q(d_ff_1_q));  // open: Qn, preset, en, reset
  not not_1 (out_2, d_ff_1_q);
endmodule

module Flip_Flop_D_subida (
  input  D,
  output Q,
  output nQ
);

  wire CLK_out, nand_1_out, nand_2_out;

  Clock CLK (.out(CLK_out));
  nand nand_1 (nand_1_out, D, CLK_out);
  nand nand_2 (nand_2_out, CLK_out, ~D);  // NAND_Gate
  nand nand_3 (Q, nand_1_out, nQ);
  nand nand_4 (nQ, Q, nand_2_out);

  // Notes on the sheet:
  //   O flip flop tipo D serve para guardar um valor.
endmodule

module \Circuito_de_9_à_0  (
  input  Q3,
  input  Q2,
  input  Q1,
  input  Q0,
  output S3,
  output S2,
  output S1,
  output S0
);

  wire and_1_out, and_2_out, and_3_out, and_4_out, and_5_out, and_6_out, and_7_out, and_8_out, and_9_out,
       not_1_out, not_2_out, not_3_out, not_4_out, not_5_out, not_6_out, not_7_out, not_8_out, not_9_out,
       not_10_out;

  not not_1 (not_1_out, Q3);
  not not_2 (not_2_out, Q2);
  not not_3 (not_3_out, Q1);
  not not_4 (not_4_out, Q0);
  not not_5 (not_5_out, Q1);
  not not_6 (not_6_out, Q0);
  not not_7 (not_7_out, Q1);
  not not_8 (not_8_out, Q0);
  not not_9 (not_9_out, Q1);
  not not_10 (not_10_out, Q0);
  not not_11 (S0, Q0);
  and and_1 (and_1_out, not_1_out, not_2_out, not_3_out, not_4_out);
  and and_2 (and_2_out, Q3, Q0);
  and and_3 (and_3_out, Q3, Q1);
  and and_4 (and_4_out, Q2, Q0);
  and and_5 (and_5_out, Q2, Q1);
  and and_6 (and_6_out, Q3, not_5_out, not_6_out);
  and and_7 (and_7_out, Q1, Q0);
  and and_8 (and_8_out, Q2, not_7_out, not_8_out);
  and and_9 (and_9_out, Q3, not_9_out, not_10_out);
  or or_1 (S3, and_1_out, and_2_out, and_3_out);
  or or_2 (S2, and_4_out, and_5_out, and_6_out);
  or or_3 (S1, and_7_out, and_8_out, and_9_out);

  // Notes on the sheet:
  //   Circuito para usar no contador de 0 à 9
endmodule

module \Circuito_de_5_à_0  (
  input  Q3,
  input  Q2,
  input  Q1,
  output S3,
  output S2,
  output S1
);

  wire and_1_out, and_2_out, and_3_out, and_4_out, not_1_out, not_2_out, not_3_out, not_4_out;

  not not_1 (not_1_out, Q3);
  not not_2 (not_2_out, Q2);
  not not_3 (not_3_out, Q1);
  not not_4 (not_4_out, Q1);
  not not_5 (S1, Q1);
  and and_1 (and_1_out, not_1_out, not_2_out, not_3_out);
  and and_2 (and_2_out, Q3, Q1);
  and and_3 (and_3_out, Q2, Q1);
  and and_4 (and_4_out, Q3, not_4_out);
  or or_1 (S3, and_1_out, and_2_out);
  or or_2 (S2, and_3_out, and_4_out);
endmodule

module QUANDO_FOR_0_de_9 (
  input  Q3,
  input  Q2,
  input  Q1,
  input  Q0,
  output S4,
  output S3,
  output S2,
  output S1,
  output S0
);

  wire and_1_out, and_2_out, and_3_out, and_4_out, and_5_out, and_6_out, and_8_out, and_9_out, not_1_out,
       not_2_out, not_3_out, not_4_out, not_5_out, not_6_out, not_7_out, not_8_out, not_9_out, not_10_out,
       not_11_out;

  not not_1 (not_1_out, Q3);
  not not_2 (not_2_out, Q2);
  not not_3 (not_3_out, Q1);
  not not_4 (not_4_out, Q3);
  not not_5 (not_5_out, Q2);
  not not_6 (not_6_out, Q1);
  not not_7 (not_7_out, Q0);
  and and_1 (and_1_out, Q2, Q0);
  and and_2 (and_2_out, Q2, Q1);
  and and_3 (and_3_out, Q3, not_8_out);
  not not_8 (not_8_out, Q0);
  and and_4 (and_4_out, Q1, Q0);
  not not_9 (not_9_out, Q1);
  and and_5 (and_5_out, Q2, not_9_out, not_10_out);
  not not_10 (not_10_out, Q0);
  and and_6 (and_6_out, Q3, not_11_out);
  not not_11 (not_11_out, Q0);
  not not_12 (S0, Q0);
  and and_7 (S4, not_1_out, not_2_out, not_3_out, Q0);
  and and_8 (and_8_out, not_4_out, not_5_out, not_6_out, not_7_out);
  or or_1 (S3, and_8_out, and_9_out);
  and and_9 (and_9_out, Q3, Q0);
  or or_2 (S2, and_1_out, and_2_out, and_3_out);
  or or_3 (S1, and_4_out, and_5_out, and_6_out);
endmodule

module quando_for_0_de_5 (
  input  Q2,
  input  Q1,
  input  Q0,
  output S3,
  output S2,
  output S1,
  output S0
);

  wire and_2_out, and_3_out, and_4_out, and_5_out, not_1_out, not_2_out, not_3_out, not_4_out, not_5_out,
       not_6_out;

  not not_1 (not_1_out, Q2);
  not not_2 (not_2_out, Q1);
  not not_3 (not_3_out, Q2);
  not not_4 (not_4_out, Q1);
  not not_5 (not_5_out, Q0);
  not not_6 (not_6_out, Q0);
  not not_7 (S0, Q0);
  and and_1 (S3, not_1_out, not_2_out, Q0);
  and and_2 (and_2_out, not_3_out, not_4_out, not_5_out);
  and and_3 (and_3_out, Q2, Q0);
  and and_4 (and_4_out, Q1, Q0);
  and and_5 (and_5_out, Q2, not_6_out);
  or or_1 (S2, and_2_out, and_3_out);
  or or_2 (S1, and_4_out, and_5_out);
endmodule

module \Contador_de_9_à_0_unidade_seg_e_min  (
  input  CLOCK,
  input  tempo,
  input  MOD,
  input  ENABLE,
  input  CLEAR,
  output saida_de_0,
  output [3:0] out_7,
  output out_8,
  output out_9,
  output out_10,
  output out_11
);

  wire d_ff_1_q, d_ff_2_q, d_ff_3_q, d_ff_4_q, multiplexer_1_out, not_1_out;

  Multiplexer multiplexer_1 (.in0(CLOCK), .in1(tempo), .out(multiplexer_1_out), .sel(not_1_out));  // open: en
  not not_1 (not_1_out, MOD);
  D_Flip_Flop d_ff_1 (
    .clk(multiplexer_1_out), .D(out_7[3]), .Q(d_ff_1_q), .Qn(out_11), .en(ENABLE), .reset(CLEAR));  // open: preset
  D_Flip_Flop d_ff_2 (
    .clk(multiplexer_1_out), .D(out_7[2]), .Q(d_ff_2_q), .Qn(out_10), .en(ENABLE));  // open: preset, reset
  D_Flip_Flop d_ff_3 (
    .clk(multiplexer_1_out), .D(out_7[1]), .Q(d_ff_3_q), .Qn(out_9), .en(ENABLE));  // open: preset, reset
  QUANDO_FOR_0_de_9 quando_for_0_de_9_1 (
    .Q3(d_ff_1_q), .Q2(d_ff_2_q), .Q1(d_ff_3_q), .Q0(d_ff_4_q), .S4(saida_de_0), .S3(out_7[3]),
    .S2(out_7[2]), .S1(out_7[1]), .S0(out_7[0]));
  D_Flip_Flop d_ff_4 (
    .clk(multiplexer_1_out), .D(out_7[0]), .Q(d_ff_4_q), .Qn(out_8), .en(ENABLE), .reset(CLEAR));  // open: preset
  Hex_Digit_Display hex_digit_display_1 (.value(out_7));  // open: dp

  // Notes on the sheet:
  //   3
  //   QUnado apertar o start ele comeca a contar
  //   unidades de segundos e minutos
  //   2
  //   1
  //   Quando o mode tá em 1 o relógio funciona com o clock normal, se vai ta normal ou no config
  //   E quando o start vai pra 1, ele fica parado e não responde nem ao clock nem ao botão de alterar
  //   0
  //   Quando vai pra 0, o relógio para de mudar com o clock e você pode apertar o "tempo" pra editar, função de chaveamento 
endmodule

module \Contador_de_5_à_0_dezena_dos_minutos  (
  input  CLK,
  input  CLK_2,
  input  CLK_3,
  input  CLOCK,
  input  tempo,
  input  MOD,
  input  Clear,
  input  enable,
  output Sinal_de_0,
  output [3:0] out_10,
  output SAIDA_3,
  output SAIDA_2,
  output SAIDA_1
);

  wire and_1_out, d_ff_1_q, d_ff_2_q, d_ff_3_q, multiplexer_1_out, not_1_out;

  and and_1 (and_1_out, CLK, CLK_2, CLK_3, CLOCK);
  not not_1 (not_1_out, MOD);
  Multiplexer multiplexer_1 (.in0(and_1_out), .in1(tempo), .out(multiplexer_1_out), .sel(not_1_out));  // open: en
  D_Flip_Flop d_ff_1 (
    .clk(multiplexer_1_out), .D(out_10[0]), .Q(d_ff_1_q), .Qn(SAIDA_1), .en(enable), .reset(Clear));  // open: preset
  D_Flip_Flop d_ff_2 (
    .clk(multiplexer_1_out), .D(out_10[1]), .Q(d_ff_2_q), .Qn(SAIDA_2), .en(enable), .reset(Clear));  // open: preset
  D_Flip_Flop d_ff_3 (
    .clk(multiplexer_1_out), .D(out_10[2]), .Q(d_ff_3_q), .Qn(SAIDA_3), .en(enable), .reset(Clear));  // open: preset
  quando_for_0_de_5 quando_for_0_de_5_1 (
    .Q2(d_ff_3_q), .Q1(d_ff_2_q), .Q0(d_ff_1_q), .S3(Sinal_de_0), .S2(out_10[2]), .S1(out_10[1]),
    .S0(out_10[0]));
  Hex_Digit_Display hex_digit_display_1 (.value({1'b0, out_10[2:0]}));  // open: dp

  assign out_10[3] = 1'b0;

  // Notes on the sheet:
  //   dezena dos minutos
  //   vez do jogador 
  //   se o jogo esta rodando
  //   se a entrada anterior ficou menor que 0
endmodule

module \Copia_do_0_à_9_unidade_de_minutos  (
  input  CLK,
  input  CLK_2,
  input  CLOCK,
  input  tempo,
  input  MOD,
  input  CLEAR,
  input  ENABLE,
  output saida_de_0,
  output [3:0] out_9,
  output SAIDA_3,
  output SAIDA_2,
  output SAIDA_1,
  output SAIDA_0
);

  wire and_1_out, d_ff_1_q, d_ff_2_q, d_ff_3_q, d_ff_4_q, multiplexer_1_out, not_1_out;

  and and_1 (and_1_out, CLK, CLK_2, CLOCK);
  not not_1 (not_1_out, MOD);
  Multiplexer multiplexer_1 (.in0(and_1_out), .in1(tempo), .out(multiplexer_1_out), .sel(not_1_out));  // open: en
  D_Flip_Flop d_ff_1 (
    .clk(multiplexer_1_out), .D(out_9[3]), .Q(d_ff_1_q), .Qn(SAIDA_0), .en(ENABLE), .reset(CLEAR));  // open: preset
  D_Flip_Flop d_ff_2 (
    .clk(multiplexer_1_out), .D(out_9[2]), .Q(d_ff_2_q), .Qn(SAIDA_1), .en(ENABLE), .reset(CLEAR));  // open: preset
  QUANDO_FOR_0_de_9 quando_for_0_de_9_1 (
    .Q3(d_ff_1_q), .Q2(d_ff_2_q), .Q1(d_ff_3_q), .Q0(d_ff_4_q), .S4(saida_de_0), .S3(out_9[3]),
    .S2(out_9[2]), .S1(out_9[1]), .S0(out_9[0]));
  D_Flip_Flop d_ff_3 (
    .clk(multiplexer_1_out), .D(out_9[1]), .Q(d_ff_3_q), .Qn(SAIDA_2), .en(ENABLE), .reset(CLEAR));  // open: preset
  D_Flip_Flop d_ff_4 (
    .clk(multiplexer_1_out), .D(out_9[0]), .Q(d_ff_4_q), .Qn(SAIDA_3), .en(ENABLE), .reset(CLEAR));  // open: preset
  Hex_Digit_Display hex_digit_display_1 (.value(out_9));  // open: dp

  // Notes on the sheet:
  //   unidades de  minutos
endmodule

module CIRCUITO_0_15 (
  input  E,
  input  CLOCK,
  input  RESET,
  output [3:0] out_4
);

  wire and_1_out, and_2_out, and_3_out, and_4_out, and_5_out, and_6_out, and_7_out, and_8_out, and_9_out,
       and_10_out, and_11_out, and_12_out, and_13_out, and_14_out, clock_1_out, not_1_out, not_2_out,
       not_3_out, not_4_out, not_5_out, not_6_out, not_7_out, not_8_out, not_9_out, not_10_out, not_11_out,
       not_12_out, not_13_out, not_14_out, or_1_out, or_2_out, or_3_out, or_4_out;

  not not_1 (not_1_out, E);
  not not_2 (not_2_out, out_4[2]);
  not not_3 (not_3_out, out_4[1]);
  not not_4 (not_4_out, out_4[0]);
  not not_5 (not_5_out, out_4[3]);
  not not_6 (not_6_out, E);
  not not_7 (not_7_out, out_4[1]);
  not not_8 (not_8_out, out_4[0]);
  not not_9 (not_9_out, out_4[2]);
  not not_10 (not_10_out, E);
  not not_11 (not_11_out, out_4[0]);
  not not_12 (not_12_out, out_4[1]);
  not not_13 (not_13_out, E);
  not not_14 (not_14_out, out_4[0]);
  and and_1 (and_1_out, not_1_out, out_4[3]);
  and and_2 (and_2_out, out_4[3], not_2_out);
  and and_3 (and_3_out, out_4[3], not_3_out);
  and and_4 (and_4_out, out_4[3], not_4_out);
  and and_5 (and_5_out, E, not_5_out, out_4[2], out_4[1], out_4[0]);
  and and_6 (and_6_out, not_6_out, out_4[2]);
  and and_7 (and_7_out, out_4[2], not_7_out);
  and and_8 (and_8_out, out_4[2], not_8_out);
  and and_9 (and_9_out, E, not_9_out, out_4[1], out_4[0]);
  and and_10 (and_10_out, not_10_out, out_4[1]);
  and and_11 (and_11_out, out_4[1], not_11_out);
  and and_12 (and_12_out, E, not_12_out, out_4[0]);
  and and_13 (and_13_out, not_13_out, out_4[0]);
  and and_14 (and_14_out, E, not_14_out);
  or or_1 (or_1_out, and_1_out, and_2_out, and_3_out, and_4_out, and_5_out);
  or or_2 (or_2_out, and_6_out, and_7_out, and_8_out, and_9_out);
  or or_3 (or_3_out, and_10_out, and_11_out, and_12_out);
  or or_4 (or_4_out, and_13_out, and_14_out);
  Clock clock_1 (.out(clock_1_out));
  D_Flip_Flop d_ff_1 (.clk(clock_1_out), .D(or_1_out), .Q(out_4[3]), .reset(RESET));  // open: Qn, preset, en
  D_Flip_Flop d_ff_2 (.clk(clock_1_out), .D(or_2_out), .Q(out_4[2]), .reset(RESET));  // open: Qn, preset, en
  D_Flip_Flop d_ff_3 (.clk(clock_1_out), .D(or_3_out), .Q(out_4[1]), .reset(RESET));  // open: Qn, preset, en
  D_Flip_Flop d_ff_4 (.clk(clock_1_out), .D(or_4_out), .Q(out_4[0]), .reset(RESET));  // open: Qn, preset, en
  Hex_Digit_Display hex_digit_display_1 (.value(out_4));  // open: dp
endmodule

module atraso (
  input  in_1,
  output out_2
);

  wire not_1_out, not_2_out, not_3_out, not_4_out, not_5_out, not_6_out, not_7_out, not_8_out, not_9_out,
       not_10_out, not_11_out, not_12_out, not_13_out, not_14_out, not_15_out;

  not not_1 (not_1_out, not_2_out);
  not not_2 (not_2_out, in_1);
  not not_3 (not_3_out, not_1_out);
  not not_4 (not_4_out, not_5_out);
  not not_5 (not_5_out, not_3_out);
  not not_6 (not_6_out, not_4_out);
  not not_7 (not_7_out, not_6_out);
  not not_8 (not_8_out, not_7_out);
  not not_9 (not_9_out, not_10_out);
  not not_10 (not_10_out, not_8_out);
  not not_11 (not_11_out, not_9_out);
  not not_12 (not_12_out, not_13_out);
  not not_13 (not_13_out, not_11_out);
  not not_14 (not_14_out, not_12_out);
  not not_15 (not_15_out, not_14_out);
  not not_16 (out_2, not_15_out);
endmodule

module comparador_de_igual_4_bits (
  input  [3:0] A,
  input  [3:0] B,
  output Igual
);

  wire igual_1_s, igual_2_s, igual_3_s, igual_4_s;

  Igual igual_1 (.A(A[0]), .B(B[0]), .S(igual_1_s));
  Igual igual_2 (.A(A[1]), .B(B[1]), .S(igual_2_s));
  Igual igual_3 (.A(A[2]), .B(B[2]), .S(igual_3_s));
  Igual igual_4 (.A(A[3]), .B(B[3]), .S(igual_4_s));
  and and_1 (Igual, igual_1_s, igual_2_s, igual_3_s, igual_4_s);
endmodule

module placar (
  input  Clock,
  input  Clear,
  input  Jogador,
  output Igual,
  output [3:0] Placar
);

  wire [3:0] adder_1_out;

  Adder #(.width(4)) adder_1 (.a(Placar), .b({3'b000, Jogador}), .out(adder_1_out));  // open: cin, cout
  Comparator #(.width(4)) comparator_1 (.a(4'b1111), .b(adder_1_out), .eq(Igual));  // open: gt, lt
  Register #(.width(4)) register_1 (.D(adder_1_out), .Q(Placar), .clk(Clock), .clr(Clear));  // open: en
  Hex_Digit_Display hex_digit_display_1 (.value(Placar));  // open: dp
endmodule

module \Comparação  (
  input  in_1,
  input  in_2,
  input  in_3,
  output out_4
);

  wire and_1_out, and_2_out, or_1_out;

  and and_1 (and_1_out, in_1, in_2);
  Counter #(.width(1), .max('h1)) counter_1 (.D(out_4), .Q(out_4), .clk(or_1_out));  // open: load, count, carry, clr
  or or_1 (or_1_out, and_1_out, and_2_out);
  and and_2 (and_2_out, ~in_2, in_3);  // AND_Gate
endmodule

module circuito_0_3 (
  input  in_1,
  output out_2
);

  wire and_1_out, and_2_out, and_3_out, and_4_out, clock_1_out, comparador_de_igual_4_bits_2_igual, d_ff_1_q,
       igual, not_1_out, not_2_out, not_3_out, not_4_out, or_1_out, or_2_out;
  wire [3:0] d_ff_5_q;

  or or_1 (or_1_out, in_1, igual);
  D_Flip_Flop d_ff_1 (.clk(or_1_out), .D(not_1_out), .Q(d_ff_1_q));  // open: Qn, preset, en, reset
  not not_1 (not_1_out, d_ff_1_q);
  and and_1 (and_1_out, d_ff_1_q, d_ff_5_q[1]);
  and and_2 (and_2_out, d_ff_1_q, d_ff_5_q[0]);
  not not_2 (not_2_out, and_1_out);
  not not_3 (not_3_out, and_2_out);
  not not_4 (not_4_out, and_2_out);
  and and_3 (and_3_out, not_2_out, and_2_out);
  and and_4 (and_4_out, and_1_out, not_3_out);
  Clock clock_1 (.out(clock_1_out));
  or or_2 (or_2_out, and_3_out, and_4_out);
  D_Flip_Flop d_ff_2 (.clk(clock_1_out), .D(1'b0), .Q(d_ff_5_q[3]));  // open: Qn, preset, en, reset
  D_Flip_Flop d_ff_3 (.clk(clock_1_out), .D(1'b0), .Q(d_ff_5_q[2]));  // open: Qn, preset, en, reset
  D_Flip_Flop d_ff_4 (.clk(clock_1_out), .D(or_2_out), .Q(d_ff_5_q[1]));  // open: Qn, preset, en, reset
  D_Flip_Flop d_ff_5 (.clk(clock_1_out), .D(not_4_out), .Q(d_ff_5_q[0]));  // open: Qn, preset, en, reset
  Hex_Digit_Display hex_digit_display_1 (.value(d_ff_5_q));  // open: dp
  comparador_de_igual_4_bits comparador_de_igual_4_bits_1 (.A(d_ff_5_q), .B(4'b0011), .Igual(igual));
  comparador_de_igual_4_bits comparador_de_igual_4_bits_2 (
    .A(d_ff_5_q), .B(4'b0001), .Igual(comparador_de_igual_4_bits_2_igual));
  not not_5 (out_2, comparador_de_igual_4_bits_2_igual);
endmodule

module contador_0_a_7 (
  input  in_1,
  output out_2
);

  wire and_1_out, and_2_out, and_3_out, and_4_out, and_5_out, and_6_out, and_7_out, and_8_out, clock_1_out,
       comparador_de_igual_4_bits_2_igual, d_ff_1_q, igual, not_1_out, not_2_out, not_3_out, not_4_out,
       not_5_out, not_6_out, not_7_out, or_1_out, or_2_out, or_3_out, S1, S2, S3, S4;

  or or_1 (or_1_out, in_1, igual);
  not not_1 (not_1_out, d_ff_1_q);
  D_Flip_Flop d_ff_1 (.clk(or_1_out), .D(not_1_out), .Q(d_ff_1_q));  // open: Qn, preset, en, reset
  and and_1 (and_1_out, d_ff_1_q, S2);
  and and_2 (and_2_out, d_ff_1_q, S3);
  and and_3 (and_3_out, d_ff_1_q, S4);
  not not_2 (not_2_out, and_1_out);
  not not_3 (not_3_out, and_2_out);
  not not_4 (not_4_out, and_3_out);
  not not_5 (not_5_out, and_2_out);
  not not_6 (not_6_out, and_3_out);
  not not_7 (not_7_out, and_3_out);
  and and_4 (and_4_out, not_2_out, and_2_out, and_3_out);
  and and_5 (and_5_out, and_1_out, not_3_out);
  and and_6 (and_6_out, and_1_out, not_4_out);
  and and_7 (and_7_out, not_5_out, and_3_out);
  and and_8 (and_8_out, and_2_out, not_6_out);
  Clock clock_1 (.out(clock_1_out));
  or or_2 (or_2_out, and_4_out, and_5_out, and_6_out);
  or or_3 (or_3_out, and_7_out, and_8_out);
  D_Flip_Flop d_ff_2 (.clk(clock_1_out), .D(1'b0), .Q(S1));  // open: Qn, preset, en, reset
  D_Flip_Flop d_ff_3 (.clk(clock_1_out), .D(or_2_out), .Q(S2));  // open: Qn, preset, en, reset
  D_Flip_Flop d_ff_4 (.clk(clock_1_out), .D(or_3_out), .Q(S3));  // open: Qn, preset, en, reset
  D_Flip_Flop d_ff_5 (.clk(clock_1_out), .D(not_7_out), .Q(S4));  // open: Qn, preset, en, reset
  Hex_Digit_Display hex_digit_display_1 (.value({S1, S2, S3, S4}));  // open: dp
  comparador_de_igual_4_bits comparador_de_igual_4_bits_1 (.A({S1, S2, S3, S4}), .B(4'b0111), .Igual(igual));
  comparador_de_igual_4_bits comparador_de_igual_4_bits_2 (
    .A({S1, S2, S3, S4}), .B(4'b0001), .Igual(comparador_de_igual_4_bits_2_igual));
  not not_8 (out_2, comparador_de_igual_4_bits_2_igual);
endmodule
